// Logisim project 1.1.4_XOR.circ as structural Verilog: 1 circuit, main circuit main
module main (
  input  in_1,
  input  in_2,
  output out_3
);

  wire nand_1_out, nor_1_out, not_1_out;

  nor nor_1 (nor_1_out, in_1, in_2);
  nand nand_1 (nand_1_out, in_1, in_2);
  not not_1 (not_1_out, nand_1_out);
  nor nor_2 (out_3, nor_1_out, not_1_out);
endmodule
