// Logisim project 1.1.7_XNOR.circ as structural Verilog: 1 circuit, main circuit main
module main (
  input  A,
  input  B,
  output out_3
);

  wire transistor_1_out;

  Transistor transistor_1 (.in(1'b1), .out(transistor_1_out), .gate(A));
  Transistor #(.\type ("n")) transistor_2 (.in(1'b0), .out(transistor_1_out), .gate(A));
  Transistor #(.\type ("n")) transistor_3 (.in(A), .out(out_3), .gate(B));
  Transistor transistor_4 (.in(transistor_1_out), .out(out_3), .gate(B));
  Transistor #(.\type ("n")) transistor_5 (.in(B), .out(out_3), .gate(A));
  Transistor transistor_6 (.in(B), .out(out_3), .gate(transistor_1_out));
endmodule
