// Logisim project 1.1.9_Decoder_2-4.circ as structural Verilog: 1 circuit, main circuit Decoder_2to4
module Decoder_2to4 (
  input  a1,
  input  a0,
  output y3,
  output y2,
  output y1,
  output y0
);

  wire not_1_out, not_2_out;

  not not_1 (not_1_out, a0);
  not not_2 (not_2_out, a1);
  and and_1 (y0, not_1_out, not_2_out);
  and and_2 (y1, not_2_out, a0);
  and and_3 (y2, not_1_out, a1);
  and and_4 (y3, a0, a1);
endmodule
