// Logisim project 1.1.b_7-Segment_ctl.circ as structural Verilog: 12 circuits, main circuit main
module main (
  input  in_1,
  input  in_2,
  input  in_3,
  input  in_4
);

  wire [15:0] decoder_4to16_1_y;

  Decoder_4to16 decoder_4to16_1 (.A3(in_1), .A2(in_2), .A1(in_3), .A0(in_4), .Y(decoder_4to16_1_y));
  _7_Segment_Display u_7_segment_display_1 ();  // open: g, f, a, b, e, d, c, dp
endmodule

module Decoder_2to4 (
  input  A1,
  input  A0,
  output Y3,
  output Y2,
  output Y1,
  output Y0
);

  wire not_1_out, not_2_out;

  not not_1 (not_1_out, A1);
  not not_2 (not_2_out, A0);
  and and_1 (Y3, A1, A0);
  and and_2 (Y2, A1, not_2_out);
  and and_3 (Y1, not_1_out, A0);
  and and_4 (Y0, not_1_out, not_2_out);
endmodule

module Decoder_3to8 (
  input  A2,
  input  A1,
  input  A0,
  output Y7,
  output Y6,
  output Y5,
  output Y4,
  output Y3,
  output Y2,
  output Y1,
  output Y0
);

  wire decoder_2to4_1_y0, decoder_2to4_1_y1, decoder_2to4_1_y2, decoder_2to4_1_y3, decoder_2to4_2_y0,
       decoder_2to4_2_y1, decoder_2to4_2_y2, decoder_2to4_2_y3, not_1_out;

  not not_1 (not_1_out, A2);
  Decoder_2to4 decoder_2to4_1 (
    .A1(A1), .A0(A0), .Y3(decoder_2to4_1_y3), .Y2(decoder_2to4_1_y2), .Y1(decoder_2to4_1_y1),
    .Y0(decoder_2to4_1_y0));
  Decoder_2to4 decoder_2to4_2 (
    .A1(A1), .A0(A0), .Y3(decoder_2to4_2_y3), .Y2(decoder_2to4_2_y2), .Y1(decoder_2to4_2_y1),
    .Y0(decoder_2to4_2_y0));
  and and_1 (Y7, decoder_2to4_1_y3, A2);
  and and_2 (Y6, decoder_2to4_1_y2, A2);
  and and_3 (Y5, decoder_2to4_1_y1, A2);
  and and_4 (Y4, decoder_2to4_1_y0, A2);
  and and_5 (Y3, decoder_2to4_2_y3, not_1_out);
  and and_6 (Y2, decoder_2to4_2_y2, not_1_out);
  and and_7 (Y1, decoder_2to4_2_y1, not_1_out);
  and and_8 (Y0, decoder_2to4_2_y0, not_1_out);
endmodule

module Decoder_4to16 (
  input  A3,
  input  A2,
  input  A1,
  input  A0,
  output [15:0] Y
);

  wire [7:0] decoder_3to8_1_y0, decoder_3to8_2_y0;
  wire [7:7] not_1_out;

  not not_1 (not_1_out[7], A3);
  Decoder_3to8 decoder_3to8_1 (
    .A2(A2), .A1(A1), .A0(A0), .Y7(decoder_3to8_1_y0[7]), .Y6(decoder_3to8_1_y0[6]),
    .Y5(decoder_3to8_1_y0[5]), .Y4(decoder_3to8_1_y0[4]), .Y3(decoder_3to8_1_y0[3]),
    .Y2(decoder_3to8_1_y0[2]), .Y1(decoder_3to8_1_y0[1]), .Y0(decoder_3to8_1_y0[0]));
  Decoder_3to8 decoder_3to8_2 (
    .A2(A2), .A1(A1), .A0(A0), .Y7(decoder_3to8_2_y0[7]), .Y6(decoder_3to8_2_y0[6]),
    .Y5(decoder_3to8_2_y0[5]), .Y4(decoder_3to8_2_y0[4]), .Y3(decoder_3to8_2_y0[3]),
    .Y2(decoder_3to8_2_y0[2]), .Y1(decoder_3to8_2_y0[1]), .Y0(decoder_3to8_2_y0[0]));
  assign Y[15:8] = {8{A3}} & decoder_3to8_1_y0;  // AND_Gate and_1, 8 bits wide
  assign Y[7:0] = decoder_3to8_2_y0 & {8{not_1_out[7]}};  // AND_Gate and_2, 8 bits wide
endmodule

module Seg_ctl (
);

  Seg_A seg_a_1 ();  // open: a9, a8, a7, a6, a5, a3, a2, a0, sego
endmodule

module Seg_A (
  input  a9,
  input  a8,
  input  a7,
  input  a6,
  input  a5,
  input  a3,
  input  a2,
  input  a0,
  output sego
);

  wire or_1_out, or_2_out, or_3_out, or_4_out, or_5_out, or_6_out;

  or or_1 (or_1_out, a2, a0);
  or or_2 (or_2_out, a9, a8);
  or or_3 (or_3_out, a6, a5);
  or or_4 (or_4_out, a3, or_1_out);
  or or_5 (or_5_out, or_2_out, a7);
  or or_6 (or_6_out, or_3_out, or_4_out);
  or or_7 (sego, or_5_out, or_6_out);
endmodule

module Seg_B (
  input  a9,
  input  a8,
  input  a7,
  input  a4,
  input  a3,
  input  a2,
  input  a1,
  input  a0,
  output sego
);

  wire or_1_out, or_2_out, or_3_out, or_4_out, or_5_out, or_6_out;

  or or_1 (or_1_out, a1, a0);
  or or_2 (or_2_out, a9, a8);
  or or_3 (or_3_out, a4, a3);
  or or_4 (or_4_out, a2, or_1_out);
  or or_5 (or_5_out, or_2_out, a7);
  or or_6 (or_6_out, or_3_out, or_4_out);
  or or_7 (sego, or_5_out, or_6_out);
endmodule

module Seg_C (
  input  a9,
  input  a8,
  input  a7,
  input  a4,
  input  a3,
  input  a1,
  input  a0,
  output sego
);

  wire or_1_out, or_2_out, or_3_out, or_4_out, or_5_out;

  or or_1 (or_1_out, a9, a8);
  or or_2 (or_2_out, a4, a3);
  or or_3 (or_3_out, a1, a0);
  or or_4 (or_4_out, or_1_out, a7);
  or or_5 (or_5_out, or_2_out, or_3_out);
  or or_6 (sego, or_4_out, or_5_out);
endmodule

module Seg_D (
  input  a9,
  input  a8,
  input  a6,
  input  a5,
  input  a3,
  input  a2,
  input  a0,
  output sego
);

  wire or_1_out, or_2_out, or_3_out, or_4_out, or_5_out;

  or or_1 (or_1_out, a9, a8);
  or or_2 (or_2_out, a5, a3);
  or or_3 (or_3_out, a2, a0);
  or or_4 (or_4_out, or_1_out, a6);
  or or_5 (or_5_out, or_2_out, or_3_out);
  or or_6 (sego, or_4_out, or_5_out);
endmodule

module Seg_E (
  input  a8,
  input  a6,
  input  a2,
  input  a0,
  output sego
);

  wire or_1_out, or_2_out;

  or or_1 (or_1_out, a8, a6);
  or or_2 (or_2_out, a2, a0);
  or or_3 (sego, or_1_out, or_2_out);
endmodule

module Seg_F (
  input  a8,
  input  a6,
  input  a5,
  input  a4,
  input  a2,
  input  a0,
  output sego
);

  wire or_1_out, or_2_out, or_3_out, or_4_out;

  or or_1 (or_1_out, a8, a6);
  or or_2 (or_2_out, a4, a2);
  or or_3 (or_3_out, or_1_out, a5);
  or or_4 (or_4_out, or_2_out, a0);
  or or_5 (sego, or_3_out, or_4_out);
endmodule

module Seg_G (
  input  a8,
  input  a6,
  input  a5,
  input  a4,
  input  a3,
  output sego
);

  wire or_1_out, or_2_out, or_3_out;

  or or_1 (or_1_out, a8, a6);
  or or_2 (or_2_out, or_1_out, a5);
  or or_3 (or_3_out, a4, a3);
  or or_4 (sego, or_2_out, or_3_out);
endmodule
