// Logisim project 1.1.c_7-Segment_ctl2.circ as structural Verilog: 13 circuits, main circuit x_Decoder_2to4
module Segment_ctl2 (
  input  a3,
  input  a2,
  input  a1,
  input  a0
);

  wire seg_ctl2_1_segctl_a, seg_ctl2_1_segctl_b, seg_ctl2_1_segctl_c, seg_ctl2_1_segctl_d,
       seg_ctl2_1_segctl_e, seg_ctl2_1_segctl_f, seg_ctl2_1_segctl_g;
  wire [15:0] x_decoder_4to16_1_y;

  x_Decoder_4to16 x_decoder_4to16_1 (.A3(a3), .A2(a2), .A1(a1), .A0(a0), .Y(x_decoder_4to16_1_y));
  Seg_ctl2 seg_ctl2_1 (
    .a15(x_decoder_4to16_1_y[15]), .a14(x_decoder_4to16_1_y[14]), .a13(x_decoder_4to16_1_y[13]),
    .a12(x_decoder_4to16_1_y[12]), .a11(x_decoder_4to16_1_y[11]), .a10(x_decoder_4to16_1_y[10]),
    .a9(x_decoder_4to16_1_y[9]), .a8(x_decoder_4to16_1_y[8]), .a7(x_decoder_4to16_1_y[7]),
    .a6(x_decoder_4to16_1_y[6]), .a5(x_decoder_4to16_1_y[5]), .a4(x_decoder_4to16_1_y[4]),
    .a3(x_decoder_4to16_1_y[3]), .a2(x_decoder_4to16_1_y[2]), .a1(x_decoder_4to16_1_y[1]),
    .a0(x_decoder_4to16_1_y[0]), .segctl_d(seg_ctl2_1_segctl_d), .segctl_a(seg_ctl2_1_segctl_a),
    .segctl_e(seg_ctl2_1_segctl_e), .segctl_b(seg_ctl2_1_segctl_b), .segctl_f(seg_ctl2_1_segctl_f),
    .segctl_c(seg_ctl2_1_segctl_c), .segctl_g(seg_ctl2_1_segctl_g));
  _7_Segment_Display u_7_segment_display_1 (
    .g(seg_ctl2_1_segctl_g), .f(seg_ctl2_1_segctl_f), .a(seg_ctl2_1_segctl_a), .b(seg_ctl2_1_segctl_b),
    .e(seg_ctl2_1_segctl_e), .d(seg_ctl2_1_segctl_d), .c(seg_ctl2_1_segctl_c));  // open: dp
endmodule

module x_Decoder_2to4 (
  input  A1,
  input  A0,
  output Y3,
  output Y2,
  output Y1,
  output Y0
);

  wire not_1_out, not_2_out;

  not not_1 (not_1_out, A1);
  not not_2 (not_2_out, A0);
  and and_1 (Y3, A1, A0);
  and and_2 (Y2, A1, not_2_out);
  and and_3 (Y1, not_1_out, A0);
  and and_4 (Y0, not_1_out, not_2_out);
endmodule

module x_Decoder_3to8 (
  input  A2,
  input  A1,
  input  A0,
  output Y7,
  output Y6,
  output Y5,
  output Y4,
  output Y3,
  output Y2,
  output Y1,
  output Y0
);

  wire not_1_out, x_decoder_2to4_1_y0, x_decoder_2to4_1_y1, x_decoder_2to4_1_y2, x_decoder_2to4_1_y3,
       x_decoder_2to4_2_y0, x_decoder_2to4_2_y1, x_decoder_2to4_2_y2, x_decoder_2to4_2_y3;

  not not_1 (not_1_out, A2);
  x_Decoder_2to4 x_decoder_2to4_1 (
    .A1(A1), .A0(A0), .Y3(x_decoder_2to4_1_y3), .Y2(x_decoder_2to4_1_y2), .Y1(x_decoder_2to4_1_y1),
    .Y0(x_decoder_2to4_1_y0));
  x_Decoder_2to4 x_decoder_2to4_2 (
    .A1(A1), .A0(A0), .Y3(x_decoder_2to4_2_y3), .Y2(x_decoder_2to4_2_y2), .Y1(x_decoder_2to4_2_y1),
    .Y0(x_decoder_2to4_2_y0));
  and and_1 (Y7, x_decoder_2to4_1_y3, A2);
  and and_2 (Y6, x_decoder_2to4_1_y2, A2);
  and and_3 (Y5, x_decoder_2to4_1_y1, A2);
  and and_4 (Y4, x_decoder_2to4_1_y0, A2);
  and and_5 (Y3, x_decoder_2to4_2_y3, not_1_out);
  and and_6 (Y2, x_decoder_2to4_2_y2, not_1_out);
  and and_7 (Y1, x_decoder_2to4_2_y1, not_1_out);
  and and_8 (Y0, x_decoder_2to4_2_y0, not_1_out);
endmodule

module x_Decoder_4to16 (
  input  A3,
  input  A2,
  input  A1,
  input  A0,
  output [15:0] Y
);

  wire [7:0] x_decoder_3to8_1_y0, x_decoder_3to8_2_y0;
  wire [7:7] not_1_out;

  not not_1 (not_1_out[7], A3);
  x_Decoder_3to8 x_decoder_3to8_1 (
    .A2(A2), .A1(A1), .A0(A0), .Y7(x_decoder_3to8_1_y0[7]), .Y6(x_decoder_3to8_1_y0[6]),
    .Y5(x_decoder_3to8_1_y0[5]), .Y4(x_decoder_3to8_1_y0[4]), .Y3(x_decoder_3to8_1_y0[3]),
    .Y2(x_decoder_3to8_1_y0[2]), .Y1(x_decoder_3to8_1_y0[1]), .Y0(x_decoder_3to8_1_y0[0]));
  x_Decoder_3to8 x_decoder_3to8_2 (
    .A2(A2), .A1(A1), .A0(A0), .Y7(x_decoder_3to8_2_y0[7]), .Y6(x_decoder_3to8_2_y0[6]),
    .Y5(x_decoder_3to8_2_y0[5]), .Y4(x_decoder_3to8_2_y0[4]), .Y3(x_decoder_3to8_2_y0[3]),
    .Y2(x_decoder_3to8_2_y0[2]), .Y1(x_decoder_3to8_2_y0[1]), .Y0(x_decoder_3to8_2_y0[0]));
  assign Y[15:8] = {8{A3}} & x_decoder_3to8_1_y0;  // AND_Gate and_1, 8 bits wide
  assign Y[7:0] = x_decoder_3to8_2_y0 & {8{not_1_out[7]}};  // AND_Gate and_2, 8 bits wide
endmodule

module Seg_ctl2 (
  input  a15,
  input  a14,
  input  a13,
  input  a12,
  input  a11,
  input  a10,
  input  a9,
  input  a8,
  input  a7,
  input  a6,
  input  a5,
  input  a4,
  input  a3,
  input  a2,
  input  a1,
  input  a0,
  output segctl_d,
  output segctl_a,
  output segctl_e,
  output segctl_b,
  output segctl_f,
  output segctl_c,
  output segctl_g
);

  Seg2_B seg2_b_1 (
    .a9(a9), .a8(a8), .a7(a7), .a4(a4), .a3(a3), .a2(a2), .a1(a1), .a0(a0), .a13(a13), .a10(a10),
    .sego(segctl_b));
  Seg2_C seg2_c_1 (
    .a9(a9), .a8(a8), .a7(a7), .a6(a6), .a5(a5), .a4(a4), .a3(a3), .a1(a1), .a0(a0), .a13(a13), .a11(a11),
    .a10(a10), .sego(segctl_c));
  Seg2_A seg2_a_1 (
    .a9(a9), .a8(a8), .a7(a7), .a6(a6), .a5(a5), .a3(a3), .a2(a2), .a0(a0), .a15(a15), .a14(a14), .a12(a12),
    .a10(a10), .sego(segctl_a));
  Seg2_D seg2_d_1 (
    .a9(a9), .a8(a8), .a6(a6), .a5(a5), .a3(a3), .a2(a2), .a0(a0), .a14(a14), .a13(a13), .a12(a12),
    .a11(a11), .sego(segctl_d));
  Seg2_E seg2_e_1 (
    .a8(a8), .a6(a6), .a2(a2), .a0(a0), .a15(a15), .a14(a14), .a13(a13), .a12(a12), .a11(a11), .a10(a10),
    .sego(segctl_e));
  Seg2_F seg2_f_1 (
    .a8(a8), .a6(a6), .a5(a5), .a4(a4), .a2(1'b0), .a0(a0), .a9(a9), .a15(a15), .a14(a14), .a12(a12),
    .a11(a11), .a10(a10), .sego(segctl_f));
  Seg2_G seg2_g_1 (
    .a8(a8), .a6(a6), .a5(a5), .a4(a4), .a3(a3), .a2(a2), .a9(a9), .a15(a15), .a14(a14), .a13(a13),
    .a11(a11), .a10(a10), .sego(segctl_g));
endmodule

module Seg2_A (
  input  a9,
  input  a8,
  input  a7,
  input  a6,
  input  a5,
  input  a3,
  input  a2,
  input  a0,
  input  a15,
  input  a14,
  input  a12,
  input  a10,
  output sego
);

  wire or_1_out, or_2_out, or_3_out, or_4_out, or_5_out, or_6_out, or_7_out, or_8_out, or_9_out, or_10_out;

  or or_1 (or_1_out, a15, a14);
  or or_2 (or_2_out, a12, a10);
  or or_3 (or_3_out, a2, a0);
  or or_4 (or_4_out, or_1_out, or_2_out);
  or or_5 (or_5_out, a9, a8);
  or or_6 (or_6_out, a6, a5);
  or or_7 (or_7_out, a3, or_8_out);
  or or_8 (or_8_out, or_3_out, or_4_out);
  or or_9 (or_9_out, or_5_out, a7);
  or or_10 (or_10_out, or_6_out, or_7_out);
  or or_11 (sego, or_9_out, or_10_out);
endmodule

module Seg2_B (
  input  a9,
  input  a8,
  input  a7,
  input  a4,
  input  a3,
  input  a2,
  input  a1,
  input  a0,
  input  a13,
  input  a10,
  output sego
);

  wire or_1_out, or_2_out, or_3_out, or_4_out, or_5_out, or_6_out, or_7_out, or_8_out;

  or or_1 (or_1_out, a1, a0);
  or or_2 (or_2_out, a13, a10);
  or or_3 (or_3_out, or_1_out, or_2_out);
  or or_4 (or_4_out, a9, a8);
  or or_5 (or_5_out, a4, a3);
  or or_6 (or_6_out, a2, or_3_out);
  or or_7 (or_7_out, or_4_out, a7);
  or or_8 (or_8_out, or_5_out, or_6_out);
  or or_9 (sego, or_7_out, or_8_out);
endmodule

module Seg2_C (
  input  a9,
  input  a8,
  input  a7,
  input  a6,
  input  a5,
  input  a4,
  input  a3,
  input  a1,
  input  a0,
  input  a13,
  input  a11,
  input  a10,
  output sego
);

  wire or_1_out, or_2_out, or_3_out, or_4_out, or_5_out, or_6_out, or_7_out, or_8_out, or_9_out, or_10_out;

  or or_1 (or_1_out, a13, a11);
  or or_2 (or_2_out, a6, a5);
  or or_3 (or_3_out, or_1_out, a10);
  or or_4 (or_4_out, or_2_out, a9);
  or or_5 (or_5_out, or_4_out, a8);
  or or_6 (or_6_out, a4, a3);
  or or_7 (or_7_out, a1, or_8_out);
  or or_8 (or_8_out, a0, or_3_out);
  or or_9 (or_9_out, or_5_out, a7);
  or or_10 (or_10_out, or_6_out, or_7_out);
  or or_11 (sego, or_9_out, or_10_out);
endmodule

module Seg2_D (
  input  a9,
  input  a8,
  input  a6,
  input  a5,
  input  a3,
  input  a2,
  input  a0,
  input  a14,
  input  a13,
  input  a12,
  input  a11,
  output sego
);

  wire or_1_out, or_2_out, or_3_out, or_4_out, or_5_out, or_6_out, or_7_out, or_8_out, or_9_out;

  or or_1 (or_1_out, a14, a13);
  or or_2 (or_2_out, a12, a11);
  or or_3 (or_3_out, or_1_out, or_2_out);
  or or_4 (or_4_out, a9, a8);
  or or_5 (or_5_out, a5, a3);
  or or_6 (or_6_out, a2, or_7_out);
  or or_7 (or_7_out, a0, or_3_out);
  or or_8 (or_8_out, or_4_out, a6);
  or or_9 (or_9_out, or_5_out, or_6_out);
  or or_10 (sego, or_8_out, or_9_out);
endmodule

module Seg2_E (
  input  a8,
  input  a6,
  input  a2,
  input  a0,
  input  a15,
  input  a14,
  input  a13,
  input  a12,
  input  a11,
  input  a10,
  output sego
);

  wire or_1_out, or_2_out, or_3_out;

  or or_1 (or_1_out, a0, a15, a14, a13, a12, a11, a10);
  or or_2 (or_2_out, a8, a6);
  or or_3 (or_3_out, a2, or_1_out);
  or or_4 (sego, or_2_out, or_3_out);
endmodule

module Seg2_F (
  input  a8,
  input  a6,
  input  a5,
  input  a4,
  input  a2,
  input  a0,
  input  a9,
  input  a15,
  input  a14,
  input  a12,
  input  a11,
  input  a10,
  output sego
);

  wire or_1_out, or_2_out, or_3_out, or_4_out, or_5_out, or_6_out;

  or or_1 (or_1_out, a9, a0);
  or or_2 (or_2_out, a8, a6);
  or or_3 (or_3_out, a4, a2);
  or or_4 (or_4_out, or_1_out, a15, a14, a12, a11, a10);
  or or_5 (or_5_out, or_2_out, a5);
  or or_6 (or_6_out, or_3_out, or_4_out);
  or or_7 (sego, or_5_out, or_6_out);
endmodule

module Seg2_G (
  input  a8,
  input  a6,
  input  a5,
  input  a4,
  input  a3,
  input  a2,
  input  a9,
  input  a15,
  input  a14,
  input  a13,
  input  a11,
  input  a10,
  output sego
);

  wire or_1_out, or_2_out, or_3_out, or_4_out, or_5_out, or_6_out;

  or or_1 (or_1_out, a2, a9);
  or or_2 (or_2_out, or_1_out, a15, a14, a13, a11, a10);
  or or_3 (or_3_out, a8, a6);
  or or_4 (or_4_out, a3, or_2_out);
  or or_5 (or_5_out, or_3_out, a5);
  or or_6 (or_6_out, a4, or_4_out);
  or or_7 (sego, or_5_out, or_6_out);
endmodule

module Seg2_H (
  input  a15,
  input  a14,
  input  a13,
  input  a12,
  input  a11,
  input  a10,
  output sego
);

  wire or_1_out, or_2_out, or_3_out, or_4_out;

  or or_1 (or_1_out, a15, a14);
  or or_2 (or_2_out, a12, a11);
  or or_3 (or_3_out, or_1_out, a13);
  or or_4 (or_4_out, or_2_out, a10);
  or or_5 (sego, or_3_out, or_4_out);
endmodule
