// Logisim project 1.1.d_Encoder_16-4.circ as structural Verilog: 1 circuit, main circuit main
module main (
  input  a15,
  input  a14,
  input  a13,
  input  a12,
  input  a11,
  input  a10,
  input  a9,
  input  a8,
  input  a7,
  input  a6,
  input  a5,
  input  a4,
  input  a3,
  input  a2,
  input  a1,
  input  a0,
  output y3,
  output y2,
  output y1,
  output y0
);

  wire or_2_out, or_3_out, or_4_out, or_5_out;

  or or_1 (y0, a15, a13, a11, a9, a7, a5, a3, a1);
  or or_2 (or_2_out, a15, a14, a13, a12);
  or or_3 (or_3_out, a11, a10, a9, a8);
  or or_4 (or_4_out, a15, a14, a11, a10);
  or or_5 (or_5_out, a7, a6, a3, a2);
  or or_6 (y3, or_2_out, or_3_out);
  or or_7 (y2, or_2_out, a7, a6, a5, a4);
  or or_8 (y1, or_4_out, or_5_out);
endmodule
