// Logisim project 1.1.e_Encoder_pri_4-2.circ as structural Verilog: 1 circuit, main circuit main
module main (
  input  a3,
  input  a2,
  input  a1,
  input  a0,
  output y1,
  output y0
);

  wire and_1_out, and_2_out, nor_1_out, not_1_out;

  not not_1 (not_1_out, a3);
  nor nor_1 (nor_1_out, a3, a2);
  and and_1 (and_1_out, not_1_out, a2);
  and and_2 (and_2_out, nor_1_out, a1);
  or or_1 (y1, a3, and_1_out);
  or or_2 (y0, a3, and_2_out);
endmodule
