// Logisim project 1.1.f_Encoder_pri_16-4.circ as structural Verilog: 3 circuits, main circuit Encoder_pri_4to2
module Encoder_pri_4to2 (
  input  a3,
  input  a2,
  input  a1,
  input  a0,
  output y1,
  output y0
);

  wire and_1_out, and_2_out, nor_1_out, not_1_out;

  not not_1 (not_1_out, a3);
  nor nor_1 (nor_1_out, a3, a2);
  and and_1 (and_1_out, not_1_out, a2);
  and and_2 (and_2_out, nor_1_out, a1);
  or or_1 (y1, a3, and_1_out);
  or or_2 (y0, a3, and_2_out);
endmodule

module Encoder_pri_8to3 (
  input  a7,
  input  a6,
  input  a5,
  input  a4,
  input  a3,
  input  a2,
  input  a1,
  input  a0,
  output y2,
  output y1,
  output y0
);

  wire and_1_out, and_2_out, and_3_out, and_4_out, encoder_pri_4to2_1_y0, encoder_pri_4to2_1_y1,
       encoder_pri_4to2_2_y0, encoder_pri_4to2_2_y1, nor_1_out;

  nor nor_1 (nor_1_out, a7, a6, a5, a4);
  not not_1 (y2, nor_1_out);
  Encoder_pri_4to2 encoder_pri_4to2_1 (
    .a3(a7), .a2(a6), .a1(a5), .a0(a4), .y1(encoder_pri_4to2_1_y1), .y0(encoder_pri_4to2_1_y0));
  Encoder_pri_4to2 encoder_pri_4to2_2 (
    .a3(a3), .a2(a2), .a1(a1), .a0(a0), .y1(encoder_pri_4to2_2_y1), .y0(encoder_pri_4to2_2_y0));
  and and_1 (and_1_out, y2, encoder_pri_4to2_1_y1);
  and and_2 (and_2_out, y2, encoder_pri_4to2_1_y0);
  and and_3 (and_3_out, nor_1_out, encoder_pri_4to2_2_y1);
  and and_4 (and_4_out, nor_1_out, encoder_pri_4to2_2_y0);
  or or_1 (y1, and_1_out, and_3_out);
  or or_2 (y0, and_2_out, and_4_out);
endmodule

module Encoder_pri_16to4 (
  input  a15,
  input  a14,
  input  a13,
  input  a12,
  input  a11,
  input  a10,
  input  a9,
  input  a8,
  input  a7,
  input  a6,
  input  a5,
  input  a4,
  input  a3,
  input  a2,
  input  a1,
  input  a0,
  output y3,
  output y2,
  output y1,
  output y0
);

  wire and_1_out, and_2_out, and_3_out, and_4_out, and_5_out, and_6_out, encoder_pri_8to3_1_y0,
       encoder_pri_8to3_1_y1, encoder_pri_8to3_1_y2, encoder_pri_8to3_2_y0, encoder_pri_8to3_2_y1,
       encoder_pri_8to3_2_y2, nor_1_out;

  nor nor_1 (nor_1_out, a15, a14, a13, a12, a11, a10, a9, a8);
  Encoder_pri_8to3 encoder_pri_8to3_1 (
    .a7(a15), .a6(a14), .a5(a13), .a4(a12), .a3(a11), .a2(a10), .a1(a9), .a0(a8), .y2(encoder_pri_8to3_1_y2),
    .y1(encoder_pri_8to3_1_y1), .y0(encoder_pri_8to3_1_y0));
  Encoder_pri_8to3 encoder_pri_8to3_2 (
    .a7(a7), .a6(a6), .a5(a5), .a4(a4), .a3(a3), .a2(a2), .a1(a1), .a0(a0), .y2(encoder_pri_8to3_2_y2),
    .y1(encoder_pri_8to3_2_y1), .y0(encoder_pri_8to3_2_y0));
  not not_1 (y3, nor_1_out);
  and and_1 (and_1_out, y3, encoder_pri_8to3_1_y2);
  and and_2 (and_2_out, nor_1_out, encoder_pri_8to3_2_y2);
  and and_3 (and_3_out, y3, encoder_pri_8to3_1_y1);
  and and_4 (and_4_out, nor_1_out, encoder_pri_8to3_2_y1);
  and and_5 (and_5_out, y3, encoder_pri_8to3_1_y0);
  and and_6 (and_6_out, nor_1_out, encoder_pri_8to3_2_y0);
  or or_1 (y2, and_1_out, and_2_out);
  or or_2 (y1, and_3_out, and_4_out);
  or or_3 (y0, and_5_out, and_6_out);
endmodule
