// Logisim project 1.1.f_Encoder_pri_16-4_ctl_7-Segment_ctl.circ as structural Verilog: 14 circuits, main circuit main
module main (
);

  wire dipswitch_1_sw1, dipswitch_1_sw2, dipswitch_1_sw3, dipswitch_1_sw4, dipswitch_1_sw5, dipswitch_1_sw6,
       dipswitch_1_sw7, dipswitch_1_sw8, dipswitch_1_sw9, dipswitch_1_sw10, dipswitch_1_sw11,
       dipswitch_1_sw12, dipswitch_1_sw13, dipswitch_1_sw14, dipswitch_1_sw15, dipswitch_1_sw16,
       encoder_pri_16to4_1_y0, encoder_pri_16to4_1_y1, encoder_pri_16to4_1_y2, encoder_pri_16to4_1_y3,
       seg_ctl_1_segctl_a, seg_ctl_1_segctl_b, seg_ctl_1_segctl_c, seg_ctl_1_segctl_d, seg_ctl_1_segctl_e,
       seg_ctl_1_segctl_f, seg_ctl_1_segctl_g;
  wire [15:0] decoder_4to16_1_y;

  DipSwitch #(.number(16)) dipswitch_1 (
    .sw1(dipswitch_1_sw1), .sw2(dipswitch_1_sw2), .sw3(dipswitch_1_sw3), .sw4(dipswitch_1_sw4),
    .sw5(dipswitch_1_sw5), .sw6(dipswitch_1_sw6), .sw7(dipswitch_1_sw7), .sw8(dipswitch_1_sw8),
    .sw9(dipswitch_1_sw9), .sw10(dipswitch_1_sw10), .sw11(dipswitch_1_sw11), .sw12(dipswitch_1_sw12),
    .sw13(dipswitch_1_sw13), .sw14(dipswitch_1_sw14), .sw15(dipswitch_1_sw15), .sw16(dipswitch_1_sw16));
  Encoder_pri_16to4 encoder_pri_16to4_1 (
    .a15(dipswitch_1_sw16), .a14(dipswitch_1_sw15), .a13(dipswitch_1_sw14), .a12(dipswitch_1_sw13),
    .a11(dipswitch_1_sw12), .a10(dipswitch_1_sw11), .a9(dipswitch_1_sw10), .a8(dipswitch_1_sw9),
    .a7(dipswitch_1_sw8), .a6(dipswitch_1_sw7), .a5(dipswitch_1_sw6), .a4(dipswitch_1_sw5),
    .a3(dipswitch_1_sw4), .a2(dipswitch_1_sw3), .a1(dipswitch_1_sw2), .a0(dipswitch_1_sw1),
    .y3(encoder_pri_16to4_1_y3), .y2(encoder_pri_16to4_1_y2), .y1(encoder_pri_16to4_1_y1),
    .y0(encoder_pri_16to4_1_y0));
  _7_Segment_Display u_7_segment_display_1 (
    .g(seg_ctl_1_segctl_g), .f(seg_ctl_1_segctl_f), .a(seg_ctl_1_segctl_a), .b(seg_ctl_1_segctl_b),
    .e(seg_ctl_1_segctl_e), .d(seg_ctl_1_segctl_d), .c(seg_ctl_1_segctl_c));  // open: dp
  Decoder_4to16 decoder_4to16_1 (
    .A3(encoder_pri_16to4_1_y3), .A2(encoder_pri_16to4_1_y2), .A1(encoder_pri_16to4_1_y1),
    .A0(encoder_pri_16to4_1_y0), .Y(decoder_4to16_1_y));
  Seg_ctl seg_ctl_1 (
    .a15(decoder_4to16_1_y[15]), .a14(decoder_4to16_1_y[14]), .a13(decoder_4to16_1_y[13]),
    .a12(decoder_4to16_1_y[12]), .a11(decoder_4to16_1_y[11]), .a10(decoder_4to16_1_y[10]),
    .a9(decoder_4to16_1_y[9]), .a8(decoder_4to16_1_y[8]), .a7(decoder_4to16_1_y[7]),
    .a6(decoder_4to16_1_y[6]), .a5(decoder_4to16_1_y[5]), .a4(decoder_4to16_1_y[4]),
    .a3(decoder_4to16_1_y[3]), .a2(decoder_4to16_1_y[2]), .a1(decoder_4to16_1_y[1]),
    .a0(decoder_4to16_1_y[0]), .segctl_d(seg_ctl_1_segctl_d), .segctl_a(seg_ctl_1_segctl_a),
    .segctl_e(seg_ctl_1_segctl_e), .segctl_b(seg_ctl_1_segctl_b), .segctl_f(seg_ctl_1_segctl_f),
    .segctl_c(seg_ctl_1_segctl_c), .segctl_g(seg_ctl_1_segctl_g));
endmodule

module Decoder_2to4 (
  input  A1,
  input  A0,
  output Y3,
  output Y2,
  output Y1,
  output Y0
);

  wire not_1_out, not_2_out;

  not not_1 (not_1_out, A1);
  not not_2 (not_2_out, A0);
  and and_1 (Y3, A1, A0);
  and and_2 (Y2, A1, not_2_out);
  and and_3 (Y1, not_1_out, A0);
  and and_4 (Y0, not_1_out, not_2_out);
endmodule

module Decoder_3to8 (
  input  A2,
  input  A1,
  input  A0,
  output Y7,
  output Y6,
  output Y5,
  output Y4,
  output Y3,
  output Y2,
  output Y1,
  output Y0
);

  wire decoder_2to4_1_y0, decoder_2to4_1_y1, decoder_2to4_1_y2, decoder_2to4_1_y3, decoder_2to4_2_y0,
       decoder_2to4_2_y1, decoder_2to4_2_y2, decoder_2to4_2_y3, not_1_out;

  not not_1 (not_1_out, A2);
  Decoder_2to4 decoder_2to4_1 (
    .A1(A1), .A0(A0), .Y3(decoder_2to4_1_y3), .Y2(decoder_2to4_1_y2), .Y1(decoder_2to4_1_y1),
    .Y0(decoder_2to4_1_y0));
  Decoder_2to4 decoder_2to4_2 (
    .A1(A1), .A0(A0), .Y3(decoder_2to4_2_y3), .Y2(decoder_2to4_2_y2), .Y1(decoder_2to4_2_y1),
    .Y0(decoder_2to4_2_y0));
  and and_1 (Y7, decoder_2to4_1_y3, A2);
  and and_2 (Y6, decoder_2to4_1_y2, A2);
  and and_3 (Y5, decoder_2to4_1_y1, A2);
  and and_4 (Y4, decoder_2to4_1_y0, A2);
  and and_5 (Y3, decoder_2to4_2_y3, not_1_out);
  and and_6 (Y2, decoder_2to4_2_y2, not_1_out);
  and and_7 (Y1, decoder_2to4_2_y1, not_1_out);
  and and_8 (Y0, decoder_2to4_2_y0, not_1_out);
endmodule

module Decoder_4to16 (
  input  A3,
  input  A2,
  input  A1,
  input  A0,
  output [15:0] Y
);

  wire [7:0] decoder_3to8_1_y0, decoder_3to8_2_y0;
  wire [7:7] not_1_out;

  not not_1 (not_1_out[7], A3);
  Decoder_3to8 decoder_3to8_1 (
    .A2(A2), .A1(A1), .A0(A0), .Y7(decoder_3to8_1_y0[7]), .Y6(decoder_3to8_1_y0[6]),
    .Y5(decoder_3to8_1_y0[5]), .Y4(decoder_3to8_1_y0[4]), .Y3(decoder_3to8_1_y0[3]),
    .Y2(decoder_3to8_1_y0[2]), .Y1(decoder_3to8_1_y0[1]), .Y0(decoder_3to8_1_y0[0]));
  Decoder_3to8 decoder_3to8_2 (
    .A2(A2), .A1(A1), .A0(A0), .Y7(decoder_3to8_2_y0[7]), .Y6(decoder_3to8_2_y0[6]),
    .Y5(decoder_3to8_2_y0[5]), .Y4(decoder_3to8_2_y0[4]), .Y3(decoder_3to8_2_y0[3]),
    .Y2(decoder_3to8_2_y0[2]), .Y1(decoder_3to8_2_y0[1]), .Y0(decoder_3to8_2_y0[0]));
  assign Y[15:8] = {8{A3}} & decoder_3to8_1_y0;  // AND_Gate and_1, 8 bits wide
  assign Y[7:0] = decoder_3to8_2_y0 & {8{not_1_out[7]}};  // AND_Gate and_2, 8 bits wide
endmodule

module Seg_ctl (
  input  a15,
  input  a14,
  input  a13,
  input  a12,
  input  a11,
  input  a10,
  input  a9,
  input  a8,
  input  a7,
  input  a6,
  input  a5,
  input  a4,
  input  a3,
  input  a2,
  input  a1,
  input  a0,
  output segctl_d,
  output segctl_a,
  output segctl_e,
  output segctl_b,
  output segctl_f,
  output segctl_c,
  output segctl_g
);

  Seg_B seg_b_1 (
    .a9(a9), .a8(a8), .a7(a7), .a4(a4), .a3(a3), .a2(a2), .a1(a1), .a0(a0), .a13(a13), .a10(a10),
    .sego(segctl_b));
  Seg_C seg_c_1 (
    .a9(a9), .a8(a8), .a7(a7), .a6(a6), .a5(a5), .a4(a4), .a3(a3), .a1(a1), .a0(a0), .a13(a13), .a11(a11),
    .a10(a10), .sego(segctl_c));
  Seg_A seg_a_1 (
    .a9(a9), .a8(a8), .a7(a7), .a6(a6), .a5(a5), .a3(a3), .a2(a2), .a0(a0), .a15(a15), .a14(a14), .a12(a12),
    .a10(a10), .sego(segctl_a));
  Seg_D seg_d_1 (
    .a9(a9), .a8(a8), .a6(a6), .a5(a5), .a3(a3), .a2(a2), .a0(a0), .a14(a14), .a13(a13), .a12(a12),
    .a11(a11), .sego(segctl_d));
  Seg_E seg_e_1 (
    .a8(a8), .a6(a6), .a2(a2), .a0(a0), .a15(a15), .a14(a14), .a13(a13), .a12(a12), .a11(a11), .a10(a10),
    .sego(segctl_e));
  Seg_F seg_f_1 (
    .a8(a8), .a6(a6), .a5(a5), .a4(a4), .a2(1'b0), .a0(a0), .a9(a9), .a15(a15), .a14(a14), .a12(a12),
    .a11(a11), .a10(a10), .sego(segctl_f));
  Seg_G seg_g_1 (
    .a8(a8), .a6(a6), .a5(a5), .a4(a4), .a3(a3), .a2(a2), .a9(a9), .a15(a15), .a14(a14), .a13(a13),
    .a11(a11), .a10(a10), .sego(segctl_g));
endmodule

module Seg_A (
  input  a9,
  input  a8,
  input  a7,
  input  a6,
  input  a5,
  input  a3,
  input  a2,
  input  a0,
  input  a15,
  input  a14,
  input  a12,
  input  a10,
  output sego
);

  wire or_1_out, or_2_out, or_3_out, or_4_out, or_5_out, or_6_out, or_7_out, or_8_out, or_9_out, or_10_out;

  or or_1 (or_1_out, a15, a14);
  or or_2 (or_2_out, a12, a10);
  or or_3 (or_3_out, a2, a0);
  or or_4 (or_4_out, or_1_out, or_2_out);
  or or_5 (or_5_out, a9, a8);
  or or_6 (or_6_out, a6, a5);
  or or_7 (or_7_out, a3, or_8_out);
  or or_8 (or_8_out, or_3_out, or_4_out);
  or or_9 (or_9_out, or_5_out, a7);
  or or_10 (or_10_out, or_6_out, or_7_out);
  or or_11 (sego, or_9_out, or_10_out);
endmodule

module Seg_B (
  input  a9,
  input  a8,
  input  a7,
  input  a4,
  input  a3,
  input  a2,
  input  a1,
  input  a0,
  input  a13,
  input  a10,
  output sego
);

  wire or_1_out, or_2_out, or_3_out, or_4_out, or_5_out, or_6_out, or_7_out, or_8_out;

  or or_1 (or_1_out, a1, a0);
  or or_2 (or_2_out, a13, a10);
  or or_3 (or_3_out, or_1_out, or_2_out);
  or or_4 (or_4_out, a9, a8);
  or or_5 (or_5_out, a4, a3);
  or or_6 (or_6_out, a2, or_3_out);
  or or_7 (or_7_out, or_4_out, a7);
  or or_8 (or_8_out, or_5_out, or_6_out);
  or or_9 (sego, or_7_out, or_8_out);
endmodule

module Seg_C (
  input  a9,
  input  a8,
  input  a7,
  input  a6,
  input  a5,
  input  a4,
  input  a3,
  input  a1,
  input  a0,
  input  a13,
  input  a11,
  input  a10,
  output sego
);

  wire or_1_out, or_2_out, or_3_out, or_4_out, or_5_out, or_6_out, or_7_out, or_8_out, or_9_out, or_10_out;

  or or_1 (or_1_out, a13, a11);
  or or_2 (or_2_out, a6, a5);
  or or_3 (or_3_out, or_1_out, a10);
  or or_4 (or_4_out, or_2_out, a9);
  or or_5 (or_5_out, or_4_out, a8);
  or or_6 (or_6_out, a4, a3);
  or or_7 (or_7_out, a1, or_8_out);
  or or_8 (or_8_out, a0, or_3_out);
  or or_9 (or_9_out, or_5_out, a7);
  or or_10 (or_10_out, or_6_out, or_7_out);
  or or_11 (sego, or_9_out, or_10_out);
endmodule

module Seg_D (
  input  a9,
  input  a8,
  input  a6,
  input  a5,
  input  a3,
  input  a2,
  input  a0,
  input  a14,
  input  a13,
  input  a12,
  input  a11,
  output sego
);

  wire or_1_out, or_2_out, or_3_out, or_4_out, or_5_out, or_6_out, or_7_out, or_8_out, or_9_out;

  or or_1 (or_1_out, a14, a13);
  or or_2 (or_2_out, a12, a11);
  or or_3 (or_3_out, or_1_out, or_2_out);
  or or_4 (or_4_out, a9, a8);
  or or_5 (or_5_out, a5, a3);
  or or_6 (or_6_out, a2, or_7_out);
  or or_7 (or_7_out, a0, or_3_out);
  or or_8 (or_8_out, or_4_out, a6);
  or or_9 (or_9_out, or_5_out, or_6_out);
  or or_10 (sego, or_8_out, or_9_out);
endmodule

module Seg_E (
  input  a8,
  input  a6,
  input  a2,
  input  a0,
  input  a15,
  input  a14,
  input  a13,
  input  a12,
  input  a11,
  input  a10,
  output sego
);

  wire or_1_out, or_2_out, or_3_out;

  or or_1 (or_1_out, a0, a15, a14, a13, a12, a11, a10);
  or or_2 (or_2_out, a8, a6);
  or or_3 (or_3_out, a2, or_1_out);
  or or_4 (sego, or_2_out, or_3_out);
endmodule

module Seg_F (
  input  a8,
  input  a6,
  input  a5,
  input  a4,
  input  a2,
  input  a0,
  input  a9,
  input  a15,
  input  a14,
  input  a12,
  input  a11,
  input  a10,
  output sego
);

  wire or_1_out, or_2_out, or_3_out, or_4_out, or_5_out, or_6_out;

  or or_1 (or_1_out, a9, a0);
  or or_2 (or_2_out, a8, a6);
  or or_3 (or_3_out, a4, a2);
  or or_4 (or_4_out, or_1_out, a15, a14, a12, a11, a10);
  or or_5 (or_5_out, or_2_out, a5);
  or or_6 (or_6_out, or_3_out, or_4_out);
  or or_7 (sego, or_5_out, or_6_out);
endmodule

module Seg_G (
  input  a8,
  input  a6,
  input  a5,
  input  a4,
  input  a3,
  input  a2,
  input  a9,
  input  a15,
  input  a14,
  input  a13,
  input  a11,
  input  a10,
  output sego
);

  wire or_1_out, or_2_out, or_3_out, or_4_out, or_5_out, or_6_out;

  or or_1 (or_1_out, a2, a9);
  or or_2 (or_2_out, or_1_out, a15, a14, a13, a11, a10);
  or or_3 (or_3_out, a8, a6);
  or or_4 (or_4_out, a3, or_2_out);
  or or_5 (or_5_out, or_3_out, a5);
  or or_6 (or_6_out, a4, or_4_out);
  or or_7 (sego, or_5_out, or_6_out);
endmodule

module Seg_H (
  input  a15,
  input  a14,
  input  a13,
  input  a12,
  input  a11,
  input  a10,
  output sego
);

  wire or_1_out, or_2_out, or_3_out, or_4_out;

  or or_1 (or_1_out, a15, a14);
  or or_2 (or_2_out, a12, a11);
  or or_3 (or_3_out, or_1_out, a13);
  or or_4 (or_4_out, or_2_out, a10);
  or or_5 (sego, or_3_out, or_4_out);
endmodule

module Encoder_16to4 (
  input  a15,
  input  a14,
  input  a13,
  input  a12,
  input  a11,
  input  a10,
  input  a9,
  input  a8,
  input  a7,
  input  a6,
  input  a5,
  input  a4,
  input  a3,
  input  a2,
  input  a1,
  input  a0,
  output y3,
  output y2,
  output y1,
  output y0
);

  wire or_2_out, or_3_out, or_4_out, or_5_out;

  or or_1 (y0, a15, a13, a11, a9, a7, a5, a3, a1);
  or or_2 (or_2_out, a15, a14, a13, a12);
  or or_3 (or_3_out, a11, a10, a9, a8);
  or or_4 (or_4_out, a15, a14, a11, a10);
  or or_5 (or_5_out, a7, a6, a3, a2);
  or or_6 (y3, or_2_out, or_3_out);
  or or_7 (y2, or_2_out, a7, a6, a5, a4);
  or or_8 (y1, or_4_out, or_5_out);
endmodule
