// Logisim project 1.2.1_mux2.circ as structural Verilog: 1 circuit, main circuit mux2
module mux2 (
  input  s,
  input  d1,
  input  d0,
  output y
);

  wire and_1_out, and_2_out, not_1_out;

  not not_1 (not_1_out, s);
  and and_1 (and_1_out, s, d1);
  and and_2 (and_2_out, d0, not_1_out);
  or or_1 (y, and_1_out, and_2_out);
endmodule
