// Logisim project 1.2.2_mux4_3bit.circ as structural Verilog: 1 circuit, main circuit mux4_3bit
module mux4_3bit (
  input  s1,
  input  s0,
  input  d3_2,
  input  d3_1,
  input  d3_0,
  input  d2_2,
  input  d2_1,
  input  d2_0,
  input  d1_2,
  input  d1_1,
  input  d1_0,
  input  d0_2,
  input  d0_1,
  input  d0_0,
  output y2,
  output y1,
  output y0
);

  wire and_1_out, and_2_out, and_3_out, and_4_out, and_5_out, and_6_out, and_7_out, and_8_out, and_9_out,
       and_10_out, and_11_out, and_12_out, decoder_2to4_1_y0, decoder_2to4_1_y1, decoder_2to4_1_y2,
       decoder_2to4_1_y3;

  Decoder_2to4 decoder_2to4_1 (
    .a1(s1), .a0(s0), .y3(decoder_2to4_1_y3), .y2(decoder_2to4_1_y2), .y1(decoder_2to4_1_y1),
    .y0(decoder_2to4_1_y0));
  and and_1 (and_1_out, d0_2, decoder_2to4_1_y0);
  and and_2 (and_2_out, d0_1, decoder_2to4_1_y0);
  and and_3 (and_3_out, d0_0, decoder_2to4_1_y0);
  and and_4 (and_4_out, d1_2, decoder_2to4_1_y1);
  and and_5 (and_5_out, d1_1, decoder_2to4_1_y1);
  and and_6 (and_6_out, d1_0, decoder_2to4_1_y1);
  and and_7 (and_7_out, d2_2, decoder_2to4_1_y2);
  and and_8 (and_8_out, d2_1, decoder_2to4_1_y2);
  and and_9 (and_9_out, d2_0, decoder_2to4_1_y2);
  and and_10 (and_10_out, d3_2, decoder_2to4_1_y3);
  and and_11 (and_11_out, d3_1, decoder_2to4_1_y3);
  and and_12 (and_12_out, d3_0, decoder_2to4_1_y3);
  or or_1 (y2, and_10_out, and_7_out, and_4_out, and_1_out);
  or or_2 (y1, and_11_out, and_8_out, and_5_out, and_2_out);
  or or_3 (y0, and_12_out, and_9_out, and_6_out, and_3_out);
endmodule
