// Logisim project 1.2.3_7-Segment_ctl3.circ as structural Verilog: 10 circuits, main circuit Segment_ctl3
module Segment_ctl3 (
  input  a3,
  input  a2,
  input  a1,
  input  a0,
  input  s
);

  wire and_1_out, multiplexer_1_out, multiplexer_2_out, multiplexer_3_out, multiplexer_4_out,
       multiplexer_5_out, multiplexer_6_out, multiplexer_7_out, not_1_out, seg_ctl2_1_segctl_a,
       seg_ctl2_1_segctl_b, seg_ctl2_1_segctl_c, seg_ctl2_1_segctl_d, seg_ctl2_1_segctl_e,
       seg_ctl2_1_segctl_f, seg_ctl2_1_segctl_g, seg_ctl_1_p4, seg_ctl_1_p5, seg_ctl_1_p6, undriven,
       undriven_2, undriven_3, undriven_4, undriven_5;
  wire [15:0] decoder_4to16_1_y;

  Decoder_4to16 decoder_4to16_1 (.A3(a3), .A2(a2), .A1(a1), .A0(a0), .Y(decoder_4to16_1_y));
  not not_1 (not_1_out, s);
  Seg_ctl2 seg_ctl2_1 (
    .a15(decoder_4to16_1_y[15]), .a14(decoder_4to16_1_y[14]), .a13(decoder_4to16_1_y[13]),
    .a12(decoder_4to16_1_y[12]), .a11(decoder_4to16_1_y[11]), .a10(decoder_4to16_1_y[10]),
    .a9(decoder_4to16_1_y[9]), .a8(decoder_4to16_1_y[8]), .a7(decoder_4to16_1_y[7]),
    .a6(decoder_4to16_1_y[6]), .a5(decoder_4to16_1_y[5]), .a4(decoder_4to16_1_y[4]),
    .a3(decoder_4to16_1_y[3]), .a2(decoder_4to16_1_y[2]), .a1(decoder_4to16_1_y[1]),
    .a0(decoder_4to16_1_y[0]), .segctl_d(seg_ctl2_1_segctl_d), .segctl_a(seg_ctl2_1_segctl_a),
    .segctl_e(seg_ctl2_1_segctl_e), .segctl_b(seg_ctl2_1_segctl_b), .segctl_f(seg_ctl2_1_segctl_f),
    .segctl_c(seg_ctl2_1_segctl_c), .segctl_g(seg_ctl2_1_segctl_g));
  // Seg_ctl seg_ctl_1: pin names not known; wires that end beside it: decoder_4to16_1_y[15], decoder_4to16_1_y[14], decoder_4to16_1_y[13], seg_ctl_1_p4, seg_ctl_1_p5, seg_ctl_1_p6
  Multiplexer multiplexer_1 (.in0(seg_ctl2_1_segctl_d), .in1(seg_ctl_1_p5), .out(multiplexer_1_out), .sel(not_1_out));
  Multiplexer multiplexer_2 (.in0(seg_ctl2_1_segctl_a), .in1(seg_ctl_1_p6), .out(multiplexer_2_out), .sel(not_1_out));
  Multiplexer multiplexer_3 (.in0(seg_ctl2_1_segctl_e), .in1(undriven_3), .out(multiplexer_3_out), .sel(not_1_out));
  Multiplexer multiplexer_4 (.in0(seg_ctl2_1_segctl_b), .in1(undriven_5), .out(multiplexer_4_out), .sel(not_1_out));
  Multiplexer multiplexer_5 (.in0(seg_ctl2_1_segctl_f), .in1(undriven_4), .out(multiplexer_5_out), .sel(not_1_out));
  Multiplexer multiplexer_6 (.in0(seg_ctl2_1_segctl_c), .in1(undriven_2), .out(multiplexer_6_out), .sel(not_1_out));
  Multiplexer multiplexer_7 (.in0(seg_ctl2_1_segctl_g), .in1(undriven), .out(multiplexer_7_out), .sel(not_1_out));
  _7_Segment_Display u_7_segment_display_1 (
    .g(multiplexer_7_out), .f(multiplexer_5_out), .a(multiplexer_2_out), .b(multiplexer_4_out),
    .e(multiplexer_3_out), .d(multiplexer_1_out), .c(multiplexer_6_out), .dp(and_1_out));
  and and_1 (and_1_out, not_1_out, seg_ctl_1_p4);
endmodule

module Seg_ctl2 (
  input  a15,
  input  a14,
  input  a13,
  input  a12,
  input  a11,
  input  a10,
  input  a9,
  input  a8,
  input  a7,
  input  a6,
  input  a5,
  input  a4,
  input  a3,
  input  a2,
  input  a1,
  input  a0,
  output segctl_d,
  output segctl_a,
  output segctl_e,
  output segctl_b,
  output segctl_f,
  output segctl_c,
  output segctl_g
);

  Seg2_B seg2_b_1 (
    .a9(a9), .a8(a8), .a7(a7), .a4(a4), .a3(a3), .a2(a2), .a1(a1), .a0(a0), .a13(a13), .a10(a10),
    .sego(segctl_b));
  Seg2_C seg2_c_1 (
    .a9(a9), .a8(a8), .a7(a7), .a6(a6), .a5(a5), .a4(a4), .a3(a3), .a1(a1), .a0(a0), .a13(a13), .a11(a11),
    .a10(a10), .sego(segctl_c));
  Seg2_A seg2_a_1 (
    .a9(a9), .a8(a8), .a7(a7), .a6(a6), .a5(a5), .a3(a3), .a2(a2), .a0(a0), .a15(a15), .a14(a14), .a12(a12),
    .a10(a10), .sego(segctl_a));
  Seg2_D seg2_d_1 (
    .a9(a9), .a8(a8), .a6(a6), .a5(a5), .a3(a3), .a2(a2), .a0(a0), .a14(a14), .a13(a13), .a12(a12),
    .a11(a11), .sego(segctl_d));
  Seg2_E seg2_e_1 (
    .a8(a8), .a6(a6), .a2(a2), .a0(a0), .a15(a15), .a14(a14), .a13(a13), .a12(a12), .a11(a11), .a10(a10),
    .sego(segctl_e));
  Seg2_F seg2_f_1 (
    .a8(a8), .a6(a6), .a5(a5), .a4(a4), .a2(1'b0), .a0(a0), .a9(a9), .a15(a15), .a14(a14), .a12(a12),
    .a11(a11), .a10(a10), .sego(segctl_f));
  Seg2_G seg2_g_1 (
    .a8(a8), .a6(a6), .a5(a5), .a4(a4), .a3(a3), .a2(a2), .a9(a9), .a15(a15), .a14(a14), .a13(a13),
    .a11(a11), .a10(a10), .sego(segctl_g));
endmodule

module Seg2_A (
  input  a9,
  input  a8,
  input  a7,
  input  a6,
  input  a5,
  input  a3,
  input  a2,
  input  a0,
  input  a15,
  input  a14,
  input  a12,
  input  a10,
  output sego
);

  wire or_1_out, or_2_out, or_3_out, or_4_out, or_5_out, or_6_out, or_7_out, or_8_out, or_9_out, or_10_out;

  or or_1 (or_1_out, a15, a14);
  or or_2 (or_2_out, a12, a10);
  or or_3 (or_3_out, a2, a0);
  or or_4 (or_4_out, or_1_out, or_2_out);
  or or_5 (or_5_out, a9, a8);
  or or_6 (or_6_out, a6, a5);
  or or_7 (or_7_out, a3, or_8_out);
  or or_8 (or_8_out, or_3_out, or_4_out);
  or or_9 (or_9_out, or_5_out, a7);
  or or_10 (or_10_out, or_6_out, or_7_out);
  or or_11 (sego, or_9_out, or_10_out);
endmodule

module Seg2_B (
  input  a9,
  input  a8,
  input  a7,
  input  a4,
  input  a3,
  input  a2,
  input  a1,
  input  a0,
  input  a13,
  input  a10,
  output sego
);

  wire or_1_out, or_2_out, or_3_out, or_4_out, or_5_out, or_6_out, or_7_out, or_8_out;

  or or_1 (or_1_out, a1, a0);
  or or_2 (or_2_out, a13, a10);
  or or_3 (or_3_out, or_1_out, or_2_out);
  or or_4 (or_4_out, a9, a8);
  or or_5 (or_5_out, a4, a3);
  or or_6 (or_6_out, a2, or_3_out);
  or or_7 (or_7_out, or_4_out, a7);
  or or_8 (or_8_out, or_5_out, or_6_out);
  or or_9 (sego, or_7_out, or_8_out);
endmodule

module Seg2_C (
  input  a9,
  input  a8,
  input  a7,
  input  a6,
  input  a5,
  input  a4,
  input  a3,
  input  a1,
  input  a0,
  input  a13,
  input  a11,
  input  a10,
  output sego
);

  wire or_1_out, or_2_out, or_3_out, or_4_out, or_5_out, or_6_out, or_7_out, or_8_out, or_9_out, or_10_out;

  or or_1 (or_1_out, a13, a11);
  or or_2 (or_2_out, a6, a5);
  or or_3 (or_3_out, or_1_out, a10);
  or or_4 (or_4_out, or_2_out, a9);
  or or_5 (or_5_out, or_4_out, a8);
  or or_6 (or_6_out, a4, a3);
  or or_7 (or_7_out, a1, or_8_out);
  or or_8 (or_8_out, a0, or_3_out);
  or or_9 (or_9_out, or_5_out, a7);
  or or_10 (or_10_out, or_6_out, or_7_out);
  or or_11 (sego, or_9_out, or_10_out);
endmodule

module Seg2_D (
  input  a9,
  input  a8,
  input  a6,
  input  a5,
  input  a3,
  input  a2,
  input  a0,
  input  a14,
  input  a13,
  input  a12,
  input  a11,
  output sego
);

  wire or_1_out, or_2_out, or_3_out, or_4_out, or_5_out, or_6_out, or_7_out, or_8_out, or_9_out;

  or or_1 (or_1_out, a14, a13);
  or or_2 (or_2_out, a12, a11);
  or or_3 (or_3_out, or_1_out, or_2_out);
  or or_4 (or_4_out, a9, a8);
  or or_5 (or_5_out, a5, a3);
  or or_6 (or_6_out, a2, or_7_out);
  or or_7 (or_7_out, a0, or_3_out);
  or or_8 (or_8_out, or_4_out, a6);
  or or_9 (or_9_out, or_5_out, or_6_out);
  or or_10 (sego, or_8_out, or_9_out);
endmodule

module Seg2_E (
  input  a8,
  input  a6,
  input  a2,
  input  a0,
  input  a15,
  input  a14,
  input  a13,
  input  a12,
  input  a11,
  input  a10,
  output sego
);

  wire or_1_out, or_2_out, or_3_out;

  or or_1 (or_1_out, a0, a15, a14, a13, a12, a11, a10);
  or or_2 (or_2_out, a8, a6);
  or or_3 (or_3_out, a2, or_1_out);
  or or_4 (sego, or_2_out, or_3_out);
endmodule

module Seg2_F (
  input  a8,
  input  a6,
  input  a5,
  input  a4,
  input  a2,
  input  a0,
  input  a9,
  input  a15,
  input  a14,
  input  a12,
  input  a11,
  input  a10,
  output sego
);

  wire or_1_out, or_2_out, or_3_out, or_4_out, or_5_out, or_6_out;

  or or_1 (or_1_out, a9, a0);
  or or_2 (or_2_out, a8, a6);
  or or_3 (or_3_out, a4, a2);
  or or_4 (or_4_out, or_1_out, a15, a14, a12, a11, a10);
  or or_5 (or_5_out, or_2_out, a5);
  or or_6 (or_6_out, or_3_out, or_4_out);
  or or_7 (sego, or_5_out, or_6_out);
endmodule

module Seg2_G (
  input  a8,
  input  a6,
  input  a5,
  input  a4,
  input  a3,
  input  a2,
  input  a9,
  input  a15,
  input  a14,
  input  a13,
  input  a11,
  input  a10,
  output sego
);

  wire or_1_out, or_2_out, or_3_out, or_4_out, or_5_out, or_6_out;

  or or_1 (or_1_out, a2, a9);
  or or_2 (or_2_out, or_1_out, a15, a14, a13, a11, a10);
  or or_3 (or_3_out, a8, a6);
  or or_4 (or_4_out, a3, or_2_out);
  or or_5 (or_5_out, or_3_out, a5);
  or or_6 (or_6_out, a4, or_4_out);
  or or_7 (sego, or_5_out, or_6_out);
endmodule

module Seg2_H (
  input  a15,
  input  a14,
  input  a13,
  input  a12,
  input  a11,
  input  a10,
  output sego
);

  wire or_1_out, or_2_out, or_3_out, or_4_out;

  or or_1 (or_1_out, a15, a14);
  or or_2 (or_2_out, a12, a11);
  or or_3 (or_3_out, or_1_out, a13);
  or or_4 (or_4_out, or_2_out, a10);
  or or_5 (sego, or_3_out, or_4_out);
endmodule
