// Logisim project 1.2.4_comp.circ as structural Verilog: 1 circuit, main circuit main
module main (
);

  wire and_1_out, dipswitch_1_sw1, dipswitch_1_sw2, dipswitch_1_sw3, dipswitch_1_sw4, dipswitch_2_sw1,
       dipswitch_2_sw2, dipswitch_2_sw3, dipswitch_2_sw4, xnor_1_out, xnor_2_out, xnor_3_out, xnor_4_out;

  DipSwitch #(.number(4)) dipswitch_1 (
    .sw1(dipswitch_1_sw1), .sw2(dipswitch_1_sw2), .sw3(dipswitch_1_sw3), .sw4(dipswitch_1_sw4));
  DipSwitch #(.number(4)) dipswitch_2 (
    .sw1(dipswitch_2_sw1), .sw2(dipswitch_2_sw2), .sw3(dipswitch_2_sw3), .sw4(dipswitch_2_sw4));
  xnor xnor_1 (xnor_1_out, dipswitch_1_sw1, dipswitch_2_sw1);
  xnor xnor_2 (xnor_2_out, dipswitch_1_sw2, dipswitch_2_sw2);
  xnor xnor_3 (xnor_3_out, dipswitch_1_sw3, dipswitch_2_sw3);
  xnor xnor_4 (xnor_4_out, dipswitch_1_sw4, dipswitch_2_sw4);
  and and_1 (and_1_out, xnor_1_out, xnor_2_out, xnor_3_out, xnor_4_out);
  LED led_1 (.in(and_1_out));
endmodule
