// Logisim project 1.2.5_full_adder_1bit.circ as structural Verilog: 1 circuit, main circuit full_adder_1bit
module full_adder_1bit (
  input  a,
  input  b,
  input  cin,
  output s,
  output cout
);

  wire and_1_out, and_2_out, xor_1_out;

  xor xor_1 (xor_1_out, a, b);
  and and_1 (and_1_out, a, b);
  and and_2 (and_2_out, xor_1_out, cin);
  xor xor_2 (s, xor_1_out, cin);
  or or_1 (cout, and_2_out, and_1_out);
endmodule
