// Logisim project 1.2.6_full_adder_1bit_2.circ as structural Verilog: 2 circuits, main circuit main
module main (
  input  a,
  input  b,
  input  cin,
  output s,
  output cout
);

  wire half_addr_1_c, half_addr_1_s, half_addr_2_c;

  half_addr half_addr_1 (.a(a), .b(b), .s(half_addr_1_s), .c(half_addr_1_c));
  half_addr half_addr_2 (.a(half_addr_1_s), .b(cin), .s(s), .c(half_addr_2_c));
  or or_1 (cout, half_addr_2_c, half_addr_1_c);
endmodule

module half_addr (
  input  a,
  input  b,
  output s,
  output c
);

  xor xor_1 (s, a, b);
  and and_1 (c, a, b);
endmodule
