// Logisim project 1.2.7_full_adder_4bit.circ as structural Verilog: 15 circuits, main circuit x_Decoder_2to4
module x_full_adder_4bit_display (
  input  a3,
  input  a2,
  input  a1,
  input  a0,
  input  b3,
  input  b2,
  input  b1,
  input  b0
);

  wire x_full_adder_4bit_1_cout, x_full_adder_4bit_1_s0, x_full_adder_4bit_1_s1, x_full_adder_4bit_1_s2,
       x_full_adder_4bit_1_s3, x_segment_ctl2_1_seg_a, x_segment_ctl2_1_seg_b, x_segment_ctl2_1_seg_c,
       x_segment_ctl2_1_seg_d, x_segment_ctl2_1_seg_e, x_segment_ctl2_1_seg_f, x_segment_ctl2_1_seg_g,
       x_segment_ctl2_2_seg_a, x_segment_ctl2_2_seg_b, x_segment_ctl2_2_seg_c, x_segment_ctl2_2_seg_d,
       x_segment_ctl2_2_seg_e, x_segment_ctl2_2_seg_f, x_segment_ctl2_2_seg_g, x_segment_ctl2_3_seg_a,
       x_segment_ctl2_3_seg_b, x_segment_ctl2_3_seg_c, x_segment_ctl2_3_seg_d, x_segment_ctl2_3_seg_e,
       x_segment_ctl2_3_seg_f, x_segment_ctl2_3_seg_g;

  x_Segment_ctl2 x_segment_ctl2_1 (
    .a3(a3), .a2(a2), .a1(a1), .a0(a0), .seg_d(x_segment_ctl2_1_seg_d), .seg_a(x_segment_ctl2_1_seg_a),
    .seg_e(x_segment_ctl2_1_seg_e), .seg_b(x_segment_ctl2_1_seg_b), .seg_f(x_segment_ctl2_1_seg_f),
    .seg_c(x_segment_ctl2_1_seg_c), .seg_g(x_segment_ctl2_1_seg_g));
  x_Segment_ctl2 x_segment_ctl2_2 (
    .a3(b3), .a2(b2), .a1(b1), .a0(b0), .seg_d(x_segment_ctl2_2_seg_d), .seg_a(x_segment_ctl2_2_seg_a),
    .seg_e(x_segment_ctl2_2_seg_e), .seg_b(x_segment_ctl2_2_seg_b), .seg_f(x_segment_ctl2_2_seg_f),
    .seg_c(x_segment_ctl2_2_seg_c), .seg_g(x_segment_ctl2_2_seg_g));
  x_full_adder_4bit x_full_adder_4bit_1 (
    .a3(a3), .a2(a2), .a1(a1), .a0(a0), .b3(b3), .b2(b2), .b1(b1), .b0(b0), .cin(1'b0),
    .s3(x_full_adder_4bit_1_s3), .s2(x_full_adder_4bit_1_s2), .s1(x_full_adder_4bit_1_s1),
    .s0(x_full_adder_4bit_1_s0), .cout(x_full_adder_4bit_1_cout));
  _7_Segment_Display u_7_segment_display_1 (
    .g(x_segment_ctl2_1_seg_g), .f(x_segment_ctl2_1_seg_f), .a(x_segment_ctl2_1_seg_a),
    .b(x_segment_ctl2_1_seg_b), .e(x_segment_ctl2_1_seg_e), .d(x_segment_ctl2_1_seg_d),
    .c(x_segment_ctl2_1_seg_c));  // open: dp
  _7_Segment_Display u_7_segment_display_2 (
    .g(x_segment_ctl2_2_seg_g), .f(x_segment_ctl2_2_seg_f), .a(x_segment_ctl2_2_seg_a),
    .b(x_segment_ctl2_2_seg_b), .e(x_segment_ctl2_2_seg_e), .d(x_segment_ctl2_2_seg_d),
    .c(x_segment_ctl2_2_seg_c));  // open: dp
  x_Segment_ctl2 x_segment_ctl2_3 (
    .a3(x_full_adder_4bit_1_s3), .a2(x_full_adder_4bit_1_s2), .a1(x_full_adder_4bit_1_s1),
    .a0(x_full_adder_4bit_1_s0), .seg_d(x_segment_ctl2_3_seg_d), .seg_a(x_segment_ctl2_3_seg_a),
    .seg_e(x_segment_ctl2_3_seg_e), .seg_b(x_segment_ctl2_3_seg_b), .seg_f(x_segment_ctl2_3_seg_f),
    .seg_c(x_segment_ctl2_3_seg_c), .seg_g(x_segment_ctl2_3_seg_g));
  _7_Segment_Display u_7_segment_display_3 (
    .g(x_segment_ctl2_3_seg_g), .f(x_segment_ctl2_3_seg_f), .a(x_segment_ctl2_3_seg_a),
    .b(x_segment_ctl2_3_seg_b), .e(x_segment_ctl2_3_seg_e), .d(x_segment_ctl2_3_seg_d),
    .c(x_segment_ctl2_3_seg_c));  // open: dp
  LED led_1 (.in(x_full_adder_4bit_1_cout));
endmodule

module x_full_adder_4bit (
  input  a3,
  input  a2,
  input  a1,
  input  a0,
  input  b3,
  input  b2,
  input  b1,
  input  b0,
  input  cin,
  output s3,
  output s2,
  output s1,
  output s0,
  output cout
);

  wire full_adder_1bit_2_cout, full_adder_1bit_3_cout, full_adder_1bit_4_cout;

  full_adder_1bit full_adder_1bit_1 (.a(a3), .b(b3), .cin(full_adder_1bit_2_cout), .s(s3), .cout(cout));
  full_adder_1bit full_adder_1bit_2 (
    .a(a2), .b(b2), .cin(full_adder_1bit_3_cout), .s(s2), .cout(full_adder_1bit_2_cout));
  full_adder_1bit full_adder_1bit_3 (
    .a(a1), .b(b1), .cin(full_adder_1bit_4_cout), .s(s1), .cout(full_adder_1bit_3_cout));
  full_adder_1bit full_adder_1bit_4 (.a(a0), .b(b0), .cin(cin), .s(s0), .cout(full_adder_1bit_4_cout));
endmodule

module x_Segment_ctl2 (
  input  a3,
  input  a2,
  input  a1,
  input  a0,
  output seg_d,
  output seg_a,
  output seg_e,
  output seg_b,
  output seg_f,
  output seg_c,
  output seg_g
);

  wire [15:0] x_decoder_4to16_1_y;

  x_Decoder_4to16 x_decoder_4to16_1 (.A3(a3), .A2(a2), .A1(a1), .A0(a0), .Y(x_decoder_4to16_1_y));
  x_Seg_ctl2 x_seg_ctl2_1 (
    .a15(x_decoder_4to16_1_y[15]), .a14(x_decoder_4to16_1_y[14]), .a13(x_decoder_4to16_1_y[13]),
    .a12(x_decoder_4to16_1_y[12]), .a11(x_decoder_4to16_1_y[11]), .a10(x_decoder_4to16_1_y[10]),
    .a9(x_decoder_4to16_1_y[9]), .a8(x_decoder_4to16_1_y[8]), .a7(x_decoder_4to16_1_y[7]),
    .a6(x_decoder_4to16_1_y[6]), .a5(x_decoder_4to16_1_y[5]), .a4(x_decoder_4to16_1_y[4]),
    .a3(x_decoder_4to16_1_y[3]), .a2(x_decoder_4to16_1_y[2]), .a1(x_decoder_4to16_1_y[1]),
    .a0(x_decoder_4to16_1_y[0]), .segctl_d(seg_d), .segctl_a(seg_a), .segctl_e(seg_e), .segctl_b(seg_b),
    .segctl_f(seg_f), .segctl_c(seg_c), .segctl_g(seg_g));
endmodule

module x_Decoder_2to4 (
  input  A1,
  input  A0,
  output Y3,
  output Y2,
  output Y1,
  output Y0
);

  wire not_1_out, not_2_out;

  not not_1 (not_1_out, A1);
  not not_2 (not_2_out, A0);
  and and_1 (Y3, A1, A0);
  and and_2 (Y2, A1, not_2_out);
  and and_3 (Y1, not_1_out, A0);
  and and_4 (Y0, not_1_out, not_2_out);
endmodule

module x_Decoder_3to8 (
  input  A2,
  input  A1,
  input  A0,
  output Y7,
  output Y6,
  output Y5,
  output Y4,
  output Y3,
  output Y2,
  output Y1,
  output Y0
);

  wire not_1_out, x_decoder_2to4_1_y0, x_decoder_2to4_1_y1, x_decoder_2to4_1_y2, x_decoder_2to4_1_y3,
       x_decoder_2to4_2_y0, x_decoder_2to4_2_y1, x_decoder_2to4_2_y2, x_decoder_2to4_2_y3;

  not not_1 (not_1_out, A2);
  x_Decoder_2to4 x_decoder_2to4_1 (
    .A1(A1), .A0(A0), .Y3(x_decoder_2to4_1_y3), .Y2(x_decoder_2to4_1_y2), .Y1(x_decoder_2to4_1_y1),
    .Y0(x_decoder_2to4_1_y0));
  x_Decoder_2to4 x_decoder_2to4_2 (
    .A1(A1), .A0(A0), .Y3(x_decoder_2to4_2_y3), .Y2(x_decoder_2to4_2_y2), .Y1(x_decoder_2to4_2_y1),
    .Y0(x_decoder_2to4_2_y0));
  and and_1 (Y7, x_decoder_2to4_1_y3, A2);
  and and_2 (Y6, x_decoder_2to4_1_y2, A2);
  and and_3 (Y5, x_decoder_2to4_1_y1, A2);
  and and_4 (Y4, x_decoder_2to4_1_y0, A2);
  and and_5 (Y3, x_decoder_2to4_2_y3, not_1_out);
  and and_6 (Y2, x_decoder_2to4_2_y2, not_1_out);
  and and_7 (Y1, x_decoder_2to4_2_y1, not_1_out);
  and and_8 (Y0, x_decoder_2to4_2_y0, not_1_out);
endmodule

module x_Decoder_4to16 (
  input  A3,
  input  A2,
  input  A1,
  input  A0,
  output [15:0] Y
);

  wire [7:0] x_decoder_3to8_1_y0, x_decoder_3to8_2_y0;
  wire [7:7] not_1_out;

  not not_1 (not_1_out[7], A3);
  x_Decoder_3to8 x_decoder_3to8_1 (
    .A2(A2), .A1(A1), .A0(A0), .Y7(x_decoder_3to8_1_y0[7]), .Y6(x_decoder_3to8_1_y0[6]),
    .Y5(x_decoder_3to8_1_y0[5]), .Y4(x_decoder_3to8_1_y0[4]), .Y3(x_decoder_3to8_1_y0[3]),
    .Y2(x_decoder_3to8_1_y0[2]), .Y1(x_decoder_3to8_1_y0[1]), .Y0(x_decoder_3to8_1_y0[0]));
  x_Decoder_3to8 x_decoder_3to8_2 (
    .A2(A2), .A1(A1), .A0(A0), .Y7(x_decoder_3to8_2_y0[7]), .Y6(x_decoder_3to8_2_y0[6]),
    .Y5(x_decoder_3to8_2_y0[5]), .Y4(x_decoder_3to8_2_y0[4]), .Y3(x_decoder_3to8_2_y0[3]),
    .Y2(x_decoder_3to8_2_y0[2]), .Y1(x_decoder_3to8_2_y0[1]), .Y0(x_decoder_3to8_2_y0[0]));
  assign Y[15:8] = {8{A3}} & x_decoder_3to8_1_y0;  // AND_Gate and_1, 8 bits wide
  assign Y[7:0] = x_decoder_3to8_2_y0 & {8{not_1_out[7]}};  // AND_Gate and_2, 8 bits wide
endmodule

module x_Seg_ctl2 (
  input  a15,
  input  a14,
  input  a13,
  input  a12,
  input  a11,
  input  a10,
  input  a9,
  input  a8,
  input  a7,
  input  a6,
  input  a5,
  input  a4,
  input  a3,
  input  a2,
  input  a1,
  input  a0,
  output segctl_d,
  output segctl_a,
  output segctl_e,
  output segctl_b,
  output segctl_f,
  output segctl_c,
  output segctl_g
);

  x_Seg2_B x_seg2_b_1 (
    .a9(a9), .a8(a8), .a7(a7), .a4(a4), .a3(a3), .a2(a2), .a1(a1), .a0(a0), .a13(a13), .a10(a10),
    .sego(segctl_b));
  x_Seg2_C x_seg2_c_1 (
    .a9(a9), .a8(a8), .a7(a7), .a6(a6), .a5(a5), .a4(a4), .a3(a3), .a1(a1), .a0(a0), .a13(a13), .a11(a11),
    .a10(a10), .sego(segctl_c));
  x_Seg2_A x_seg2_a_1 (
    .a9(a9), .a8(a8), .a7(a7), .a6(a6), .a5(a5), .a3(a3), .a2(a2), .a0(a0), .a15(a15), .a14(a14), .a12(a12),
    .a10(a10), .sego(segctl_a));
  x_Seg2_D x_seg2_d_1 (
    .a9(a9), .a8(a8), .a6(a6), .a5(a5), .a3(a3), .a2(a2), .a0(a0), .a14(a14), .a13(a13), .a12(a12),
    .a11(a11), .sego(segctl_d));
  x_Seg2_E x_seg2_e_1 (
    .a8(a8), .a6(a6), .a2(a2), .a0(a0), .a15(a15), .a14(a14), .a13(a13), .a12(a12), .a11(a11), .a10(a10),
    .sego(segctl_e));
  x_Seg2_F x_seg2_f_1 (
    .a8(a8), .a6(a6), .a5(a5), .a4(a4), .a2(1'b0), .a0(a0), .a9(a9), .a15(a15), .a14(a14), .a12(a12),
    .a11(a11), .a10(a10), .sego(segctl_f));
  x_Seg2_G x_seg2_g_1 (
    .a8(a8), .a6(a6), .a5(a5), .a4(a4), .a3(a3), .a2(a2), .a9(a9), .a15(a15), .a14(a14), .a13(a13),
    .a11(a11), .a10(a10), .sego(segctl_g));
endmodule

module x_Seg2_A (
  input  a9,
  input  a8,
  input  a7,
  input  a6,
  input  a5,
  input  a3,
  input  a2,
  input  a0,
  input  a15,
  input  a14,
  input  a12,
  input  a10,
  output sego
);

  wire or_1_out, or_2_out, or_3_out, or_4_out, or_5_out, or_6_out, or_7_out, or_8_out, or_9_out, or_10_out;

  or or_1 (or_1_out, a15, a14);
  or or_2 (or_2_out, a12, a10);
  or or_3 (or_3_out, a2, a0);
  or or_4 (or_4_out, or_1_out, or_2_out);
  or or_5 (or_5_out, a9, a8);
  or or_6 (or_6_out, a6, a5);
  or or_7 (or_7_out, a3, or_8_out);
  or or_8 (or_8_out, or_3_out, or_4_out);
  or or_9 (or_9_out, or_5_out, a7);
  or or_10 (or_10_out, or_6_out, or_7_out);
  or or_11 (sego, or_9_out, or_10_out);
endmodule

module x_Seg2_B (
  input  a9,
  input  a8,
  input  a7,
  input  a4,
  input  a3,
  input  a2,
  input  a1,
  input  a0,
  input  a13,
  input  a10,
  output sego
);

  wire or_1_out, or_2_out, or_3_out, or_4_out, or_5_out, or_6_out, or_7_out, or_8_out;

  or or_1 (or_1_out, a1, a0);
  or or_2 (or_2_out, a13, a10);
  or or_3 (or_3_out, or_1_out, or_2_out);
  or or_4 (or_4_out, a9, a8);
  or or_5 (or_5_out, a4, a3);
  or or_6 (or_6_out, a2, or_3_out);
  or or_7 (or_7_out, or_4_out, a7);
  or or_8 (or_8_out, or_5_out, or_6_out);
  or or_9 (sego, or_7_out, or_8_out);
endmodule

module x_Seg2_C (
  input  a9,
  input  a8,
  input  a7,
  input  a6,
  input  a5,
  input  a4,
  input  a3,
  input  a1,
  input  a0,
  input  a13,
  input  a11,
  input  a10,
  output sego
);

  wire or_1_out, or_2_out, or_3_out, or_4_out, or_5_out, or_6_out, or_7_out, or_8_out, or_9_out, or_10_out;

  or or_1 (or_1_out, a13, a11);
  or or_2 (or_2_out, a6, a5);
  or or_3 (or_3_out, or_1_out, a10);
  or or_4 (or_4_out, or_2_out, a9);
  or or_5 (or_5_out, or_4_out, a8);
  or or_6 (or_6_out, a4, a3);
  or or_7 (or_7_out, a1, or_8_out);
  or or_8 (or_8_out, a0, or_3_out);
  or or_9 (or_9_out, or_5_out, a7);
  or or_10 (or_10_out, or_6_out, or_7_out);
  or or_11 (sego, or_9_out, or_10_out);
endmodule

module x_Seg2_D (
  input  a9,
  input  a8,
  input  a6,
  input  a5,
  input  a3,
  input  a2,
  input  a0,
  input  a14,
  input  a13,
  input  a12,
  input  a11,
  output sego
);

  wire or_1_out, or_2_out, or_3_out, or_4_out, or_5_out, or_6_out, or_7_out, or_8_out, or_9_out;

  or or_1 (or_1_out, a14, a13);
  or or_2 (or_2_out, a12, a11);
  or or_3 (or_3_out, or_1_out, or_2_out);
  or or_4 (or_4_out, a9, a8);
  or or_5 (or_5_out, a5, a3);
  or or_6 (or_6_out, a2, or_7_out);
  or or_7 (or_7_out, a0, or_3_out);
  or or_8 (or_8_out, or_4_out, a6);
  or or_9 (or_9_out, or_5_out, or_6_out);
  or or_10 (sego, or_8_out, or_9_out);
endmodule

module x_Seg2_E (
  input  a8,
  input  a6,
  input  a2,
  input  a0,
  input  a15,
  input  a14,
  input  a13,
  input  a12,
  input  a11,
  input  a10,
  output sego
);

  wire or_1_out, or_2_out, or_3_out;

  or or_1 (or_1_out, a0, a15, a14, a13, a12, a11, a10);
  or or_2 (or_2_out, a8, a6);
  or or_3 (or_3_out, a2, or_1_out);
  or or_4 (sego, or_2_out, or_3_out);
endmodule

module x_Seg2_F (
  input  a8,
  input  a6,
  input  a5,
  input  a4,
  input  a2,
  input  a0,
  input  a9,
  input  a15,
  input  a14,
  input  a12,
  input  a11,
  input  a10,
  output sego
);

  wire or_1_out, or_2_out, or_3_out, or_4_out, or_5_out, or_6_out;

  or or_1 (or_1_out, a9, a0);
  or or_2 (or_2_out, a8, a6);
  or or_3 (or_3_out, a4, a2);
  or or_4 (or_4_out, or_1_out, a15, a14, a12, a11, a10);
  or or_5 (or_5_out, or_2_out, a5);
  or or_6 (or_6_out, or_3_out, or_4_out);
  or or_7 (sego, or_5_out, or_6_out);
endmodule

module x_Seg2_G (
  input  a8,
  input  a6,
  input  a5,
  input  a4,
  input  a3,
  input  a2,
  input  a9,
  input  a15,
  input  a14,
  input  a13,
  input  a11,
  input  a10,
  output sego
);

  wire or_1_out, or_2_out, or_3_out, or_4_out, or_5_out, or_6_out;

  or or_1 (or_1_out, a2, a9);
  or or_2 (or_2_out, or_1_out, a15, a14, a13, a11, a10);
  or or_3 (or_3_out, a8, a6);
  or or_4 (or_4_out, a3, or_2_out);
  or or_5 (or_5_out, or_3_out, a5);
  or or_6 (or_6_out, a4, or_4_out);
  or or_7 (sego, or_5_out, or_6_out);
endmodule

module x_Seg2_H (
  input  a15,
  input  a14,
  input  a13,
  input  a12,
  input  a11,
  input  a10,
  output sego
);

  wire or_1_out, or_2_out, or_3_out, or_4_out;

  or or_1 (or_1_out, a15, a14);
  or or_2 (or_2_out, a12, a11);
  or or_3 (or_3_out, or_1_out, a13);
  or or_4 (or_4_out, or_2_out, a10);
  or or_5 (sego, or_3_out, or_4_out);
endmodule
