// Logisim project 1.2.8_full_sub_4bit.circ as structural Verilog: 3 circuits, main circuit full_sub_1bit
module full_sub_4bit_display (
  input  a3,
  input  a2,
  input  a1,
  input  a0,
  input  b3,
  input  b2,
  input  b1,
  input  b0
);

  wire full_sub_4bit_1_cout, full_sub_4bit_1_d0, full_sub_4bit_1_d1, full_sub_4bit_1_d2, full_sub_4bit_1_d3,
       x_segment_ctl2_1_seg_a, x_segment_ctl2_1_seg_b, x_segment_ctl2_1_seg_c, x_segment_ctl2_1_seg_d,
       x_segment_ctl2_1_seg_e, x_segment_ctl2_1_seg_f, x_segment_ctl2_1_seg_g, x_segment_ctl2_2_seg_a,
       x_segment_ctl2_2_seg_b, x_segment_ctl2_2_seg_c, x_segment_ctl2_2_seg_d, x_segment_ctl2_2_seg_e,
       x_segment_ctl2_2_seg_f, x_segment_ctl2_2_seg_g, x_segment_ctl2_3_seg_a, x_segment_ctl2_3_seg_b,
       x_segment_ctl2_3_seg_c, x_segment_ctl2_3_seg_d, x_segment_ctl2_3_seg_e, x_segment_ctl2_3_seg_f,
       x_segment_ctl2_3_seg_g;

  x_Segment_ctl2 x_segment_ctl2_1 (
    .a3(a3), .a2(a2), .a1(a1), .a0(a0), .seg_d(x_segment_ctl2_1_seg_d), .seg_a(x_segment_ctl2_1_seg_a),
    .seg_e(x_segment_ctl2_1_seg_e), .seg_b(x_segment_ctl2_1_seg_b), .seg_f(x_segment_ctl2_1_seg_f),
    .seg_c(x_segment_ctl2_1_seg_c), .seg_g(x_segment_ctl2_1_seg_g));
  x_Segment_ctl2 x_segment_ctl2_2 (
    .a3(b3), .a2(b2), .a1(b1), .a0(b0), .seg_d(x_segment_ctl2_2_seg_d), .seg_a(x_segment_ctl2_2_seg_a),
    .seg_e(x_segment_ctl2_2_seg_e), .seg_b(x_segment_ctl2_2_seg_b), .seg_f(x_segment_ctl2_2_seg_f),
    .seg_c(x_segment_ctl2_2_seg_c), .seg_g(x_segment_ctl2_2_seg_g));
  full_sub_4bit full_sub_4bit_1 (
    .a3(a3), .a2(a2), .a1(a1), .a0(a0), .b3(b3), .b2(b2), .b1(b1), .b0(b0), .cin(1'b0),
    .d3(full_sub_4bit_1_d3), .d2(full_sub_4bit_1_d2), .d1(full_sub_4bit_1_d1), .d0(full_sub_4bit_1_d0),
    .cout(full_sub_4bit_1_cout));
  _7_Segment_Display u_7_segment_display_1 (
    .g(x_segment_ctl2_1_seg_g), .f(x_segment_ctl2_1_seg_f), .a(x_segment_ctl2_1_seg_a),
    .b(x_segment_ctl2_1_seg_b), .e(x_segment_ctl2_1_seg_e), .d(x_segment_ctl2_1_seg_d),
    .c(x_segment_ctl2_1_seg_c));  // open: dp
  _7_Segment_Display u_7_segment_display_2 (
    .g(x_segment_ctl2_2_seg_g), .f(x_segment_ctl2_2_seg_f), .a(x_segment_ctl2_2_seg_a),
    .b(x_segment_ctl2_2_seg_b), .e(x_segment_ctl2_2_seg_e), .d(x_segment_ctl2_2_seg_d),
    .c(x_segment_ctl2_2_seg_c));  // open: dp
  x_Segment_ctl2 x_segment_ctl2_3 (
    .a3(full_sub_4bit_1_d3), .a2(full_sub_4bit_1_d2), .a1(full_sub_4bit_1_d1), .a0(full_sub_4bit_1_d0),
    .seg_d(x_segment_ctl2_3_seg_d), .seg_a(x_segment_ctl2_3_seg_a), .seg_e(x_segment_ctl2_3_seg_e),
    .seg_b(x_segment_ctl2_3_seg_b), .seg_f(x_segment_ctl2_3_seg_f), .seg_c(x_segment_ctl2_3_seg_c),
    .seg_g(x_segment_ctl2_3_seg_g));
  _7_Segment_Display u_7_segment_display_3 (
    .g(x_segment_ctl2_3_seg_g), .f(x_segment_ctl2_3_seg_f), .a(x_segment_ctl2_3_seg_a),
    .b(x_segment_ctl2_3_seg_b), .e(x_segment_ctl2_3_seg_e), .d(x_segment_ctl2_3_seg_d),
    .c(x_segment_ctl2_3_seg_c));  // open: dp
  LED led_1 (.in(full_sub_4bit_1_cout));
endmodule

module full_sub_4bit (
  input  a3,
  input  a2,
  input  a1,
  input  a0,
  input  b3,
  input  b2,
  input  b1,
  input  b0,
  input  cin,
  output d3,
  output d2,
  output d1,
  output d0,
  output cout
);

  wire full_sub_1bit_2_cout, full_sub_1bit_3_cout, full_sub_1bit_4_cout;

  full_sub_1bit full_sub_1bit_1 (.a(a3), .b(b3), .cin(full_sub_1bit_2_cout), .d(d3), .cout(cout));
  full_sub_1bit full_sub_1bit_2 (.a(a2), .b(b2), .cin(full_sub_1bit_3_cout), .d(d2), .cout(full_sub_1bit_2_cout));
  full_sub_1bit full_sub_1bit_3 (.a(a1), .b(b1), .cin(full_sub_1bit_4_cout), .d(d1), .cout(full_sub_1bit_3_cout));
  full_sub_1bit full_sub_1bit_4 (.a(a0), .b(b0), .cin(cin), .d(d0), .cout(full_sub_1bit_4_cout));
endmodule

module full_sub_1bit (
  input  a,
  input  b,
  input  cin,
  output d,
  output cout
);

  wire and_1_out, and_2_out, not_1_out, not_2_out, xor_1_out;

  xor xor_1 (xor_1_out, a, b);
  not not_1 (not_1_out, a);
  not not_2 (not_2_out, xor_1_out);
  xor xor_2 (d, xor_1_out, cin);
  and and_1 (and_1_out, not_2_out, cin);
  and and_2 (and_2_out, not_1_out, b);
  or or_1 (cout, and_1_out, and_2_out);
endmodule
