// Logisim project 1.2.c_adder_4bit_two's complement.circ as structural Verilog: 19 circuits, main circuit Decoder_2to4
module full_adder_4bit_display_buma (
  input  a3,
  input  a2,
  input  a1,
  input  a0,
  input  b3,
  input  b2,
  input  b1,
  input  b0,
  input  cin,
  output y3,
  output y2,
  output y1,
  output y0,
  output cout
);

  wire and_1_out, and_2_out, and_3_out, and_4_out, bu2yuan_1_y0, bu2yuan_1_y1, bu2yuan_1_y2, bu2yuan_1_y3,
       bu2yuan_2_y0, bu2yuan_2_y1, bu2yuan_2_y2, bu2yuan_2_y3, bu2yuan_3_y0, bu2yuan_3_y1, bu2yuan_3_y2,
       bu2yuan_3_y3, or_1_out, or_2_out, or_3_out, segment_ctl2_1_seg_a, segment_ctl2_1_seg_b,
       segment_ctl2_1_seg_c, segment_ctl2_1_seg_d, segment_ctl2_1_seg_e, segment_ctl2_1_seg_f,
       segment_ctl2_1_seg_g, segment_ctl2_2_seg_a, segment_ctl2_2_seg_b, segment_ctl2_2_seg_c,
       segment_ctl2_2_seg_d, segment_ctl2_2_seg_e, segment_ctl2_2_seg_f, segment_ctl2_2_seg_g,
       segment_ctl2_3_seg_a, segment_ctl2_3_seg_b, segment_ctl2_3_seg_c, segment_ctl2_3_seg_d,
       segment_ctl2_3_seg_e, segment_ctl2_3_seg_f, segment_ctl2_3_seg_g;

  and and_1 (and_1_out, y3, ~a3, ~b3);  // AND_Gate
  and and_2 (and_2_out, ~y3, a3, b3);  // AND_Gate
  bu2yuan bu2yuan_1 (
    .a3(a3), .a2(a2), .a1(a1), .a0(a0), .y3(bu2yuan_1_y3), .y2(bu2yuan_1_y2), .y1(bu2yuan_1_y1),
    .y0(bu2yuan_1_y0));
  bu2yuan bu2yuan_2 (
    .a3(b3), .a2(b2), .a1(b1), .a0(b0), .y3(bu2yuan_2_y3), .y2(bu2yuan_2_y2), .y1(bu2yuan_2_y1),
    .y0(bu2yuan_2_y0));
  or or_1 (or_1_out, and_1_out, and_2_out);
  x_full_adder_4bit x_full_adder_4bit_1 (
    .a3(a3), .a2(a2), .a1(a1), .a0(a0), .b3(b3), .b2(b2), .b1(b1), .b0(b0), .cin(cin), .s3(y3), .s2(y2),
    .s1(y1), .s0(y0), .cout(cout));
  Segment_ctl2 segment_ctl2_1 (
    .a3(bu2yuan_1_y3), .a2(bu2yuan_1_y2), .a1(bu2yuan_1_y1), .a0(bu2yuan_1_y0), .seg_d(segment_ctl2_1_seg_d),
    .seg_a(segment_ctl2_1_seg_a), .seg_e(segment_ctl2_1_seg_e), .seg_b(segment_ctl2_1_seg_b),
    .seg_f(segment_ctl2_1_seg_f), .seg_c(segment_ctl2_1_seg_c), .seg_g(segment_ctl2_1_seg_g));
  and and_3 (and_3_out, a3, ~a2, ~a1, ~a0);  // AND_Gate
  Segment_ctl2 segment_ctl2_2 (
    .a3(bu2yuan_2_y3), .a2(bu2yuan_2_y2), .a1(bu2yuan_2_y1), .a0(bu2yuan_2_y0), .seg_d(segment_ctl2_2_seg_d),
    .seg_a(segment_ctl2_2_seg_a), .seg_e(segment_ctl2_2_seg_e), .seg_b(segment_ctl2_2_seg_b),
    .seg_f(segment_ctl2_2_seg_f), .seg_c(segment_ctl2_2_seg_c), .seg_g(segment_ctl2_2_seg_g));
  and and_4 (and_4_out, b3, ~b2, ~b1, ~b0);  // AND_Gate
  or or_2 (or_2_out, segment_ctl2_1_seg_g, and_3_out);
  or or_3 (or_3_out, segment_ctl2_2_seg_g, and_4_out);
  bu2yuan bu2yuan_3 (
    .a3(y3), .a2(y2), .a1(y1), .a0(y0), .y3(bu2yuan_3_y3), .y2(bu2yuan_3_y2), .y1(bu2yuan_3_y1),
    .y0(bu2yuan_3_y0));
  _7_Segment_Display u_7_segment_display_1 (.g(a3));  // open: f, a, b, e, d, c, dp
  _7_Segment_Display u_7_segment_display_2 (.g(b3));  // open: f, a, b, e, d, c, dp
  _7_Segment_Display u_7_segment_display_3 (
    .g(or_2_out), .f(segment_ctl2_1_seg_f), .a(segment_ctl2_1_seg_a), .b(segment_ctl2_1_seg_b),
    .e(segment_ctl2_1_seg_e), .d(segment_ctl2_1_seg_d), .c(segment_ctl2_1_seg_c));  // open: dp
  _7_Segment_Display u_7_segment_display_4 (
    .g(or_3_out), .f(segment_ctl2_2_seg_f), .a(segment_ctl2_2_seg_a), .b(segment_ctl2_2_seg_b),
    .e(segment_ctl2_2_seg_e), .d(segment_ctl2_2_seg_d), .c(segment_ctl2_2_seg_c));  // open: dp
  LED led_1 (.in(or_1_out));
  Segment_ctl2 segment_ctl2_3 (
    .a3(bu2yuan_3_y3), .a2(bu2yuan_3_y2), .a1(bu2yuan_3_y1), .a0(bu2yuan_3_y0), .seg_d(segment_ctl2_3_seg_d),
    .seg_a(segment_ctl2_3_seg_a), .seg_e(segment_ctl2_3_seg_e), .seg_b(segment_ctl2_3_seg_b),
    .seg_f(segment_ctl2_3_seg_f), .seg_c(segment_ctl2_3_seg_c), .seg_g(segment_ctl2_3_seg_g));
  _7_Segment_Display u_7_segment_display_5 (.g(y3));  // open: f, a, b, e, d, c, dp
  _7_Segment_Display u_7_segment_display_6 (
    .g(segment_ctl2_3_seg_g), .f(segment_ctl2_3_seg_f), .a(segment_ctl2_3_seg_a), .b(segment_ctl2_3_seg_b),
    .e(segment_ctl2_3_seg_e), .d(segment_ctl2_3_seg_d), .c(segment_ctl2_3_seg_c));  // open: dp

  // Notes on the sheet:
  //   led turn red meas overflow
endmodule

module full_adder_4bit_display_fanma2 (
  input  a3,
  input  a2,
  input  a1,
  input  a0,
  input  b3,
  input  b2,
  input  b1,
  input  b0
);

  wire and_1_out, and_2_out, and_3_out, and_4_out, and_5_out, and_6_out, comparator_1_gt, comparator_1_lt,
       fan2yuan_1_y0, fan2yuan_1_y1, fan2yuan_1_y2, fan2yuan_1_y3, fan2yuan_2_y0, fan2yuan_2_y1,
       fan2yuan_2_y2, fan2yuan_2_y3, nand_1_out, nor_1_out, or_1_out, or_2_out, or_3_out,
       segment_ctl2_1_seg_a, segment_ctl2_1_seg_b, segment_ctl2_1_seg_c, segment_ctl2_1_seg_d,
       segment_ctl2_1_seg_e, segment_ctl2_1_seg_f, segment_ctl2_1_seg_g, segment_ctl2_2_seg_a,
       segment_ctl2_2_seg_b, segment_ctl2_2_seg_c, segment_ctl2_2_seg_d, segment_ctl2_2_seg_e,
       segment_ctl2_2_seg_f, segment_ctl2_2_seg_g, segment_ctl2_3_seg_a, segment_ctl2_3_seg_b,
       segment_ctl2_3_seg_c, segment_ctl2_3_seg_d, segment_ctl2_3_seg_e, segment_ctl2_3_seg_f,
       segment_ctl2_3_seg_g;
  wire [1:0] encoder_4to2_1_y0;
  wire [2:0] abs_3bit_1_y0, abs_3bit_2_y0;
  wire [3:0] multiplexer_1_out, not_4_out, not_8_out, x_full_adder_4bit_1_s0, x_full_adder_4bit_2_s0;

  abs_3bit abs_3bit_1 (
    .a3(a3), .a2(a2), .a1(a1), .a0(a0), .y2(abs_3bit_1_y0[2]), .y1(abs_3bit_1_y0[1]), .y0(abs_3bit_1_y0[0]));
  abs_3bit abs_3bit_2 (
    .a3(b3), .a2(b2), .a1(b1), .a0(b0), .y2(abs_3bit_2_y0[2]), .y1(abs_3bit_2_y0[1]), .y0(abs_3bit_2_y0[0]));
  nand nand_1 (nand_1_out, a2, a1, a0, b2, b1, b0);
  and and_1 (and_1_out, a3, nand_1_out, b3);
  nor nor_1 (nor_1_out, a3, b3);
  and and_2 (and_2_out, comparator_1_gt, a3, ~b3);  // AND_Gate
  and and_3 (and_3_out, ~a3, b3, comparator_1_lt);  // AND_Gate
  or or_1 (or_1_out, and_2_out, and_3_out);
  and and_4 (and_4_out, a3, ~comparator_1_gt, ~b3);  // AND_Gate
  or or_2 (or_2_out, and_4_out, and_5_out);
  and and_5 (and_5_out, b3, ~a3, ~comparator_1_lt);  // AND_Gate
  and and_6 (and_6_out, a3, b3);
  fan2yuan fan2yuan_1 (
    .a3(a3), .a2(a2), .a1(a1), .a0(a0), .y3(fan2yuan_1_y3), .y2(fan2yuan_1_y2), .y1(fan2yuan_1_y1),
    .y0(fan2yuan_1_y0));
  Comparator #(.mode("unsigned"), .width(3)) comparator_1 (
    .a(abs_3bit_1_y0), .b(abs_3bit_2_y0), .gt(comparator_1_gt), .lt(comparator_1_lt));  // open: eq
  fan2yuan fan2yuan_2 (
    .a3(b3), .a2(b2), .a1(b1), .a0(b0), .y3(fan2yuan_2_y3), .y2(fan2yuan_2_y2), .y1(fan2yuan_2_y1),
    .y0(fan2yuan_2_y0));
  x_full_adder_4bit x_full_adder_4bit_1 (
    .a3(a3), .a2(a2), .a1(a1), .a0(a0), .b3(b3), .b2(b2), .b1(b1), .b0(b0), .cin(1'b0),
    .s3(x_full_adder_4bit_1_s0[3]), .s2(x_full_adder_4bit_1_s0[2]), .s1(x_full_adder_4bit_1_s0[1]),
    .s0(x_full_adder_4bit_1_s0[0]));  // open: cout
  or or_3 (or_3_out, and_1_out, or_1_out);
  not not_1 (not_4_out[3], x_full_adder_4bit_1_s0[3]);
  not not_2 (not_4_out[2], x_full_adder_4bit_1_s0[2]);
  not not_3 (not_4_out[1], x_full_adder_4bit_1_s0[1]);
  not not_4 (not_4_out[0], x_full_adder_4bit_1_s0[0]);
  Segment_ctl2 segment_ctl2_1 (
    .a3(1'b0), .a2(fan2yuan_1_y2), .a1(fan2yuan_1_y1), .a0(fan2yuan_1_y0), .seg_d(segment_ctl2_1_seg_d),
    .seg_a(segment_ctl2_1_seg_a), .seg_e(segment_ctl2_1_seg_e), .seg_b(segment_ctl2_1_seg_b),
    .seg_f(segment_ctl2_1_seg_f), .seg_c(segment_ctl2_1_seg_c), .seg_g(segment_ctl2_1_seg_g));
  Segment_ctl2 segment_ctl2_2 (
    .a3(1'b0), .a2(fan2yuan_2_y2), .a1(fan2yuan_2_y1), .a0(fan2yuan_2_y0), .seg_d(segment_ctl2_2_seg_d),
    .seg_a(segment_ctl2_2_seg_a), .seg_e(segment_ctl2_2_seg_e), .seg_b(segment_ctl2_2_seg_b),
    .seg_f(segment_ctl2_2_seg_f), .seg_c(segment_ctl2_2_seg_c), .seg_g(segment_ctl2_2_seg_g));
  encoder_4to2 encoder_4to2_1 (
    .a3(and_6_out), .a2(or_2_out), .a1(or_1_out), .a0(nor_1_out), .y1(encoder_4to2_1_y0[1]),
    .y0(encoder_4to2_1_y0[0]));
  x_full_adder_4bit x_full_adder_4bit_2 (
    .a3(x_full_adder_4bit_1_s0[3]), .a2(x_full_adder_4bit_1_s0[2]), .a1(x_full_adder_4bit_1_s0[1]),
    .a0(x_full_adder_4bit_1_s0[0]), .b3(1'b0), .b2(1'b0), .b1(1'b0), .b0(1'b1), .cin(1'b0),
    .s3(x_full_adder_4bit_2_s0[3]), .s2(x_full_adder_4bit_2_s0[2]), .s1(x_full_adder_4bit_2_s0[1]),
    .s0(x_full_adder_4bit_2_s0[0]));  // open: cout
  not not_5 (not_8_out[3], x_full_adder_4bit_2_s0[3]);
  not not_6 (not_8_out[2], x_full_adder_4bit_2_s0[2]);
  not not_7 (not_8_out[1], x_full_adder_4bit_2_s0[1]);
  not not_8 (not_8_out[0], x_full_adder_4bit_2_s0[0]);
  _7_Segment_Display u_7_segment_display_1 (.g(fan2yuan_1_y3));  // open: f, a, b, e, d, c, dp
  _7_Segment_Display u_7_segment_display_2 (.g(fan2yuan_2_y3));  // open: f, a, b, e, d, c, dp
  Multiplexer #(.select(2), .width(4)) multiplexer_1 (
    .in0(x_full_adder_4bit_1_s0), .in1(not_4_out), .in2(x_full_adder_4bit_2_s0), .in3(not_8_out),
    .out(multiplexer_1_out), .sel(encoder_4to2_1_y0));
  _7_Segment_Display u_7_segment_display_3 (
    .g(segment_ctl2_1_seg_g), .f(segment_ctl2_1_seg_f), .a(segment_ctl2_1_seg_a), .b(segment_ctl2_1_seg_b),
    .e(segment_ctl2_1_seg_e), .d(segment_ctl2_1_seg_d), .c(segment_ctl2_1_seg_c));  // open: dp
  _7_Segment_Display u_7_segment_display_4 (
    .g(segment_ctl2_2_seg_g), .f(segment_ctl2_2_seg_f), .a(segment_ctl2_2_seg_a), .b(segment_ctl2_2_seg_b),
    .e(segment_ctl2_2_seg_e), .d(segment_ctl2_2_seg_d), .c(segment_ctl2_2_seg_c));  // open: dp
  Segment_ctl2 segment_ctl2_3 (
    .a3(multiplexer_1_out[3]), .a2(multiplexer_1_out[2]), .a1(multiplexer_1_out[1]),
    .a0(multiplexer_1_out[0]), .seg_d(segment_ctl2_3_seg_d), .seg_a(segment_ctl2_3_seg_a),
    .seg_e(segment_ctl2_3_seg_e), .seg_b(segment_ctl2_3_seg_b), .seg_f(segment_ctl2_3_seg_f),
    .seg_c(segment_ctl2_3_seg_c), .seg_g(segment_ctl2_3_seg_g));
  _7_Segment_Display u_7_segment_display_5 (.g(or_3_out));  // open: f, a, b, e, d, c, dp
  _7_Segment_Display u_7_segment_display_6 (
    .g(segment_ctl2_3_seg_g), .f(segment_ctl2_3_seg_f), .a(segment_ctl2_3_seg_a), .b(segment_ctl2_3_seg_b),
    .e(segment_ctl2_3_seg_e), .d(segment_ctl2_3_seg_d), .c(segment_ctl2_3_seg_c));  // open: dp

  // Notes on the sheet:
  //   y3
  //   y2
  //   y1
  //   y0
endmodule

module full_adder_4bit_display_fanma (
  input  a3,
  input  a2,
  input  a1,
  input  a0,
  input  b3,
  input  b2,
  input  b1,
  input  b0
);

  wire and_1_out, and_2_out, and_3_out, and_4_out, and_5_out, and_6_out, and_7_out, and_8_out, and_9_out,
       comparator_1_gt, comparator_1_lt, fan2yuan_1_y3, fan2yuan_2_y3, full_sub_4bit_mux_1_d0,
       full_sub_4bit_mux_1_d1, full_sub_4bit_mux_1_d2, full_sub_4bit_mux_1_d3, multiplexer_1_out,
       multiplexer_2_out, multiplexer_3_out, multiplexer_4_out, or_1_out, or_2_out, or_3_out,
       segment_ctl2_1_seg_a, segment_ctl2_1_seg_b, segment_ctl2_1_seg_c, segment_ctl2_1_seg_d,
       segment_ctl2_1_seg_e, segment_ctl2_1_seg_f, segment_ctl2_1_seg_g, segment_ctl2_2_seg_a,
       segment_ctl2_2_seg_b, segment_ctl2_2_seg_c, segment_ctl2_2_seg_d, segment_ctl2_2_seg_e,
       segment_ctl2_2_seg_f, segment_ctl2_2_seg_g, segment_ctl2_3_seg_a, segment_ctl2_3_seg_b,
       segment_ctl2_3_seg_c, segment_ctl2_3_seg_d, segment_ctl2_3_seg_e, segment_ctl2_3_seg_f,
       segment_ctl2_3_seg_g, x_full_adder_4bit_1_s0, x_full_adder_4bit_1_s1, x_full_adder_4bit_1_s2,
       x_full_adder_4bit_1_s3, xnor_1_out;
  wire [2:0] fan2yuan_1_y0, fan2yuan_2_y0;

  fan2yuan fan2yuan_1 (
    .a3(b3), .a2(b2), .a1(b1), .a0(b0), .y3(fan2yuan_1_y3), .y2(fan2yuan_1_y0[2]), .y1(fan2yuan_1_y0[1]),
    .y0(fan2yuan_1_y0[0]));
  fan2yuan fan2yuan_2 (
    .a3(a3), .a2(a2), .a1(a1), .a0(a0), .y3(fan2yuan_2_y3), .y2(fan2yuan_2_y0[2]), .y1(fan2yuan_2_y0[1]),
    .y0(fan2yuan_2_y0[0]));
  or or_1 (or_1_out, fan2yuan_2_y0[2], fan2yuan_2_y0[1], fan2yuan_2_y0[0], fan2yuan_1_y0[0], fan2yuan_1_y0[0], fan2yuan_1_y0[0]);
  xnor xnor_1 (xnor_1_out, fan2yuan_2_y3, fan2yuan_1_y3);
  Comparator #(.mode("unsigned"), .width(3)) comparator_1 (
    .a(fan2yuan_2_y0), .b(fan2yuan_1_y0), .gt(comparator_1_gt), .lt(comparator_1_lt));  // open: eq
  and and_1 (and_1_out, fan2yuan_2_y3, ~fan2yuan_1_y3, ~comparator_1_gt);  // AND_Gate
  Segment_ctl2 segment_ctl2_1 (
    .a3(1'b0), .a2(fan2yuan_2_y0[2]), .a1(fan2yuan_2_y0[1]), .a0(fan2yuan_2_y0[0]),
    .seg_d(segment_ctl2_1_seg_d), .seg_a(segment_ctl2_1_seg_a), .seg_e(segment_ctl2_1_seg_e),
    .seg_b(segment_ctl2_1_seg_b), .seg_f(segment_ctl2_1_seg_f), .seg_c(segment_ctl2_1_seg_c),
    .seg_g(segment_ctl2_1_seg_g));
  Segment_ctl2 segment_ctl2_2 (
    .a3(1'b0), .a2(fan2yuan_1_y0[2]), .a1(fan2yuan_1_y0[1]), .a0(fan2yuan_1_y0[0]),
    .seg_d(segment_ctl2_2_seg_d), .seg_a(segment_ctl2_2_seg_a), .seg_e(segment_ctl2_2_seg_e),
    .seg_b(segment_ctl2_2_seg_b), .seg_f(segment_ctl2_2_seg_f), .seg_c(segment_ctl2_2_seg_c),
    .seg_g(segment_ctl2_2_seg_g));
  and and_2 (and_2_out, xnor_1_out, fan2yuan_2_y3);
  and and_3 (and_3_out, xnor_1_out, fan2yuan_1_y3);
  and and_4 (and_4_out, xnor_1_out, fan2yuan_2_y3);
  and and_5 (and_5_out, xnor_1_out, fan2yuan_1_y3);
  or or_2 (or_2_out, and_1_out, and_9_out);
  _7_Segment_Display u_7_segment_display_1 (.g(fan2yuan_2_y3));  // open: f, a, b, e, d, c, dp
  _7_Segment_Display u_7_segment_display_2 (
    .g(segment_ctl2_1_seg_g), .f(segment_ctl2_1_seg_f), .a(segment_ctl2_1_seg_a), .b(segment_ctl2_1_seg_b),
    .e(segment_ctl2_1_seg_e), .d(segment_ctl2_1_seg_d), .c(segment_ctl2_1_seg_c));  // open: dp
  and and_6 (and_6_out, fan2yuan_2_y3, or_1_out, fan2yuan_1_y3);
  _7_Segment_Display u_7_segment_display_3 (.g(fan2yuan_1_y3));  // open: f, a, b, e, d, c, dp
  _7_Segment_Display u_7_segment_display_4 (
    .g(segment_ctl2_2_seg_g), .f(segment_ctl2_2_seg_f), .a(segment_ctl2_2_seg_a), .b(segment_ctl2_2_seg_b),
    .e(segment_ctl2_2_seg_e), .d(segment_ctl2_2_seg_d), .c(segment_ctl2_2_seg_c));  // open: dp
  and and_7 (and_7_out, comparator_1_lt, and_9_out);
  and and_8 (and_8_out, fan2yuan_2_y3, ~fan2yuan_1_y3, comparator_1_gt);  // AND_Gate
  or or_3 (or_3_out, and_6_out, and_7_out, and_8_out);
  and and_9 (and_9_out, ~fan2yuan_2_y3, fan2yuan_1_y3, ~comparator_1_gt);  // AND_Gate
  x_full_adder_4bit x_full_adder_4bit_1 (
    .a3(and_2_out), .a2(fan2yuan_2_y0[2]), .a1(fan2yuan_2_y0[1]), .a0(fan2yuan_2_y0[0]), .b3(and_3_out),
    .b2(fan2yuan_1_y0[2]), .b1(fan2yuan_1_y0[1]), .b0(fan2yuan_1_y0[0]), .cin(1'b0),
    .s3(x_full_adder_4bit_1_s3), .s2(x_full_adder_4bit_1_s2), .s1(x_full_adder_4bit_1_s1),
    .s0(x_full_adder_4bit_1_s0));  // open: cout
  full_sub_4bit_mux full_sub_4bit_mux_1 (
    .a3(and_4_out), .a2(fan2yuan_2_y0[2]), .a1(fan2yuan_2_y0[1]), .a0(fan2yuan_2_y0[0]), .b3(and_5_out),
    .b2(fan2yuan_1_y0[2]), .b1(fan2yuan_1_y0[1]), .b0(fan2yuan_1_y0[0]), .cin(1'b0), .sel_b(or_2_out),
    .d3(full_sub_4bit_mux_1_d3), .d2(full_sub_4bit_mux_1_d2), .d1(full_sub_4bit_mux_1_d1),
    .d0(full_sub_4bit_mux_1_d0));  // open: cout
  _7_Segment_Display u_7_segment_display_5 (.g(or_3_out));  // open: f, a, b, e, d, c, dp
  _7_Segment_Display u_7_segment_display_6 (
    .g(segment_ctl2_3_seg_g), .f(segment_ctl2_3_seg_f), .a(segment_ctl2_3_seg_a), .b(segment_ctl2_3_seg_b),
    .e(segment_ctl2_3_seg_e), .d(segment_ctl2_3_seg_d), .c(segment_ctl2_3_seg_c));  // open: dp
  Multiplexer multiplexer_1 (
    .in0(full_sub_4bit_mux_1_d3), .in1(x_full_adder_4bit_1_s3), .out(multiplexer_1_out), .sel(xnor_1_out));
  Multiplexer multiplexer_2 (
    .in0(full_sub_4bit_mux_1_d2), .in1(x_full_adder_4bit_1_s2), .out(multiplexer_2_out), .sel(xnor_1_out));
  Multiplexer multiplexer_3 (
    .in0(full_sub_4bit_mux_1_d1), .in1(x_full_adder_4bit_1_s1), .out(multiplexer_3_out), .sel(xnor_1_out));
  Multiplexer multiplexer_4 (
    .in0(full_sub_4bit_mux_1_d0), .in1(x_full_adder_4bit_1_s0), .out(multiplexer_4_out), .sel(xnor_1_out));
  Segment_ctl2 segment_ctl2_3 (
    .a3(multiplexer_1_out), .a2(multiplexer_2_out), .a1(multiplexer_3_out), .a0(multiplexer_4_out),
    .seg_d(segment_ctl2_3_seg_d), .seg_a(segment_ctl2_3_seg_a), .seg_e(segment_ctl2_3_seg_e),
    .seg_b(segment_ctl2_3_seg_b), .seg_f(segment_ctl2_3_seg_f), .seg_c(segment_ctl2_3_seg_c),
    .seg_g(segment_ctl2_3_seg_g));
endmodule

module bu2yuan (
  input  a3,
  input  a2,
  input  a1,
  input  a0,
  output y3,
  output y2,
  output y1,
  output y0
);

  wire and_1_out, not_1_out, not_2_out, not_3_out, or_1_out, segment_ctl2_1_seg_a, segment_ctl2_1_seg_b,
       segment_ctl2_1_seg_c, segment_ctl2_1_seg_d, segment_ctl2_1_seg_e, segment_ctl2_1_seg_f,
       segment_ctl2_1_seg_g, undriven, x_full_adder_4bit_1_s0, x_full_adder_4bit_1_s1,
       x_full_adder_4bit_1_s2, x_full_adder_4bit_1_s3;

  not not_1 (not_1_out, a2);
  not not_2 (not_2_out, a1);
  not not_3 (not_3_out, a0);
  and and_1 (and_1_out, a3, ~a2, ~a1, ~a0);  // AND_Gate
  x_full_adder_4bit x_full_adder_4bit_1 (
    .a3(1'b0), .a2(not_1_out), .a1(not_2_out), .a0(not_3_out), .b3(1'b0), .b2(1'b0), .b1(1'b0), .b0(1'b1),
    .cin(undriven), .s3(x_full_adder_4bit_1_s3), .s2(x_full_adder_4bit_1_s2), .s1(x_full_adder_4bit_1_s1),
    .s0(x_full_adder_4bit_1_s0));  // open: cout
  Multiplexer multiplexer_1 (.in0(a3), .in1(x_full_adder_4bit_1_s3), .out(y3), .sel(a3));
  Multiplexer multiplexer_2 (.in0(a2), .in1(x_full_adder_4bit_1_s2), .out(y2), .sel(a3));
  Multiplexer multiplexer_3 (.in0(a1), .in1(x_full_adder_4bit_1_s1), .out(y1), .sel(a3));
  Multiplexer multiplexer_4 (.in0(a0), .in1(x_full_adder_4bit_1_s0), .out(y0), .sel(a3));
  Segment_ctl2 segment_ctl2_1 (
    .a3(y3), .a2(y2), .a1(y1), .a0(y0), .seg_d(segment_ctl2_1_seg_d), .seg_a(segment_ctl2_1_seg_a),
    .seg_e(segment_ctl2_1_seg_e), .seg_b(segment_ctl2_1_seg_b), .seg_f(segment_ctl2_1_seg_f),
    .seg_c(segment_ctl2_1_seg_c), .seg_g(segment_ctl2_1_seg_g));
  or or_1 (or_1_out, segment_ctl2_1_seg_g, and_1_out);
  _7_Segment_Display u_7_segment_display_1 (.g(a3));  // open: f, a, b, e, d, c, dp
  _7_Segment_Display u_7_segment_display_2 (
    .g(or_1_out), .f(segment_ctl2_1_seg_f), .a(segment_ctl2_1_seg_a), .b(segment_ctl2_1_seg_b),
    .e(segment_ctl2_1_seg_e), .d(segment_ctl2_1_seg_d), .c(segment_ctl2_1_seg_c));  // open: dp
endmodule

module fan2yuan (
  input  a3,
  input  a2,
  input  a1,
  input  a0,
  output y3,
  output y2,
  output y1,
  output y0
);

  wire nand_1_out, not_1_out, not_2_out, not_3_out;

  nand nand_1 (nand_1_out, a2, a1, a0);
  not not_1 (not_1_out, a2);
  not not_2 (not_2_out, a1);
  not not_3 (not_3_out, a0);
  and and_1 (y3, a3, nand_1_out);
  Multiplexer multiplexer_1 (.in0(a2), .in1(not_1_out), .out(y2), .sel(a3));
  Multiplexer multiplexer_2 (.in0(a1), .in1(not_2_out), .out(y1), .sel(a3));
  Multiplexer multiplexer_3 (.in0(a0), .in1(not_3_out), .out(y0), .sel(a3));
endmodule

module Segment_ctl2 (
  input  a3,
  input  a2,
  input  a1,
  input  a0,
  output seg_d,
  output seg_a,
  output seg_e,
  output seg_b,
  output seg_f,
  output seg_c,
  output seg_g
);

  wire [15:0] decoder_4to16_1_y;

  Decoder_4to16 decoder_4to16_1 (.A3(a3), .A2(a2), .A1(a1), .A0(a0), .Y(decoder_4to16_1_y));
  Seg_ctl2 seg_ctl2_1 (
    .a15(decoder_4to16_1_y[15]), .a14(decoder_4to16_1_y[14]), .a13(decoder_4to16_1_y[13]),
    .a12(decoder_4to16_1_y[12]), .a11(decoder_4to16_1_y[11]), .a10(decoder_4to16_1_y[10]),
    .a9(decoder_4to16_1_y[9]), .a8(decoder_4to16_1_y[8]), .a7(decoder_4to16_1_y[7]),
    .a6(decoder_4to16_1_y[6]), .a5(decoder_4to16_1_y[5]), .a4(decoder_4to16_1_y[4]),
    .a3(decoder_4to16_1_y[3]), .a2(decoder_4to16_1_y[2]), .a1(decoder_4to16_1_y[1]),
    .a0(decoder_4to16_1_y[0]), .segctl_d(seg_d), .segctl_a(seg_a), .segctl_e(seg_e), .segctl_b(seg_b),
    .segctl_f(seg_f), .segctl_c(seg_c), .segctl_g(seg_g));
endmodule

module Decoder_2to4 (
  input  A1,
  input  A0,
  output Y3,
  output Y2,
  output Y1,
  output Y0
);

  wire not_1_out, not_2_out;

  not not_1 (not_1_out, A1);
  not not_2 (not_2_out, A0);
  and and_1 (Y3, A1, A0);
  and and_2 (Y2, A1, not_2_out);
  and and_3 (Y1, not_1_out, A0);
  and and_4 (Y0, not_1_out, not_2_out);
endmodule

module Decoder_3to8 (
  input  A2,
  input  A1,
  input  A0,
  output Y7,
  output Y6,
  output Y5,
  output Y4,
  output Y3,
  output Y2,
  output Y1,
  output Y0
);

  wire decoder_2to4_1_y0, decoder_2to4_1_y1, decoder_2to4_1_y2, decoder_2to4_1_y3, decoder_2to4_2_y0,
       decoder_2to4_2_y1, decoder_2to4_2_y2, decoder_2to4_2_y3, not_1_out;

  not not_1 (not_1_out, A2);
  Decoder_2to4 decoder_2to4_1 (
    .A1(A1), .A0(A0), .Y3(decoder_2to4_1_y3), .Y2(decoder_2to4_1_y2), .Y1(decoder_2to4_1_y1),
    .Y0(decoder_2to4_1_y0));
  Decoder_2to4 decoder_2to4_2 (
    .A1(A1), .A0(A0), .Y3(decoder_2to4_2_y3), .Y2(decoder_2to4_2_y2), .Y1(decoder_2to4_2_y1),
    .Y0(decoder_2to4_2_y0));
  and and_1 (Y7, decoder_2to4_1_y3, A2);
  and and_2 (Y6, decoder_2to4_1_y2, A2);
  and and_3 (Y5, decoder_2to4_1_y1, A2);
  and and_4 (Y4, decoder_2to4_1_y0, A2);
  and and_5 (Y3, decoder_2to4_2_y3, not_1_out);
  and and_6 (Y2, decoder_2to4_2_y2, not_1_out);
  and and_7 (Y1, decoder_2to4_2_y1, not_1_out);
  and and_8 (Y0, decoder_2to4_2_y0, not_1_out);
endmodule

module Decoder_4to16 (
  input  A3,
  input  A2,
  input  A1,
  input  A0,
  output [15:0] Y
);

  wire [7:0] decoder_3to8_1_y0, decoder_3to8_2_y0;
  wire [7:7] not_1_out;

  not not_1 (not_1_out[7], A3);
  Decoder_3to8 decoder_3to8_1 (
    .A2(A2), .A1(A1), .A0(A0), .Y7(decoder_3to8_1_y0[7]), .Y6(decoder_3to8_1_y0[6]),
    .Y5(decoder_3to8_1_y0[5]), .Y4(decoder_3to8_1_y0[4]), .Y3(decoder_3to8_1_y0[3]),
    .Y2(decoder_3to8_1_y0[2]), .Y1(decoder_3to8_1_y0[1]), .Y0(decoder_3to8_1_y0[0]));
  Decoder_3to8 decoder_3to8_2 (
    .A2(A2), .A1(A1), .A0(A0), .Y7(decoder_3to8_2_y0[7]), .Y6(decoder_3to8_2_y0[6]),
    .Y5(decoder_3to8_2_y0[5]), .Y4(decoder_3to8_2_y0[4]), .Y3(decoder_3to8_2_y0[3]),
    .Y2(decoder_3to8_2_y0[2]), .Y1(decoder_3to8_2_y0[1]), .Y0(decoder_3to8_2_y0[0]));
  assign Y[15:8] = {8{A3}} & decoder_3to8_1_y0;  // AND_Gate and_1, 8 bits wide
  assign Y[7:0] = decoder_3to8_2_y0 & {8{not_1_out[7]}};  // AND_Gate and_2, 8 bits wide
endmodule

module Seg_ctl2 (
  input  a15,
  input  a14,
  input  a13,
  input  a12,
  input  a11,
  input  a10,
  input  a9,
  input  a8,
  input  a7,
  input  a6,
  input  a5,
  input  a4,
  input  a3,
  input  a2,
  input  a1,
  input  a0,
  output segctl_d,
  output segctl_a,
  output segctl_e,
  output segctl_b,
  output segctl_f,
  output segctl_c,
  output segctl_g
);

  Seg2_B seg2_b_1 (
    .a9(a9), .a8(a8), .a7(a7), .a4(a4), .a3(a3), .a2(a2), .a1(a1), .a0(a0), .a13(a13), .a10(a10),
    .sego(segctl_b));
  Seg2_C seg2_c_1 (
    .a9(a9), .a8(a8), .a7(a7), .a6(a6), .a5(a5), .a4(a4), .a3(a3), .a1(a1), .a0(a0), .a13(a13), .a11(a11),
    .a10(a10), .sego(segctl_c));
  Seg2_A seg2_a_1 (
    .a9(a9), .a8(a8), .a7(a7), .a6(a6), .a5(a5), .a3(a3), .a2(a2), .a0(a0), .a15(a15), .a14(a14), .a12(a12),
    .a10(a10), .sego(segctl_a));
  Seg2_D seg2_d_1 (
    .a9(a9), .a8(a8), .a6(a6), .a5(a5), .a3(a3), .a2(a2), .a0(a0), .a14(a14), .a13(a13), .a12(a12),
    .a11(a11), .sego(segctl_d));
  Seg2_E seg2_e_1 (
    .a8(a8), .a6(a6), .a2(a2), .a0(a0), .a15(a15), .a14(a14), .a13(a13), .a12(a12), .a11(a11), .a10(a10),
    .sego(segctl_e));
  Seg2_F seg2_f_1 (
    .a8(a8), .a6(a6), .a5(a5), .a4(a4), .a2(1'b0), .a0(a0), .a9(a9), .a15(a15), .a14(a14), .a12(a12),
    .a11(a11), .a10(a10), .sego(segctl_f));
  Seg2_G seg2_g_1 (
    .a8(a8), .a6(a6), .a5(a5), .a4(a4), .a3(a3), .a2(a2), .a9(a9), .a15(a15), .a14(a14), .a13(a13),
    .a11(a11), .a10(a10), .sego(segctl_g));
endmodule

module Seg2_A (
  input  a9,
  input  a8,
  input  a7,
  input  a6,
  input  a5,
  input  a3,
  input  a2,
  input  a0,
  input  a15,
  input  a14,
  input  a12,
  input  a10,
  output sego
);

  wire or_1_out, or_2_out, or_3_out, or_4_out, or_5_out, or_6_out, or_7_out, or_8_out, or_9_out, or_10_out;

  or or_1 (or_1_out, a15, a14);
  or or_2 (or_2_out, a12, a10);
  or or_3 (or_3_out, a2, a0);
  or or_4 (or_4_out, or_1_out, or_2_out);
  or or_5 (or_5_out, a9, a8);
  or or_6 (or_6_out, a6, a5);
  or or_7 (or_7_out, a3, or_8_out);
  or or_8 (or_8_out, or_3_out, or_4_out);
  or or_9 (or_9_out, or_5_out, a7);
  or or_10 (or_10_out, or_6_out, or_7_out);
  or or_11 (sego, or_9_out, or_10_out);
endmodule

module Seg2_B (
  input  a9,
  input  a8,
  input  a7,
  input  a4,
  input  a3,
  input  a2,
  input  a1,
  input  a0,
  input  a13,
  input  a10,
  output sego
);

  wire or_1_out, or_2_out, or_3_out, or_4_out, or_5_out, or_6_out, or_7_out, or_8_out;

  or or_1 (or_1_out, a1, a0);
  or or_2 (or_2_out, a13, a10);
  or or_3 (or_3_out, or_1_out, or_2_out);
  or or_4 (or_4_out, a9, a8);
  or or_5 (or_5_out, a4, a3);
  or or_6 (or_6_out, a2, or_3_out);
  or or_7 (or_7_out, or_4_out, a7);
  or or_8 (or_8_out, or_5_out, or_6_out);
  or or_9 (sego, or_7_out, or_8_out);
endmodule

module Seg2_C (
  input  a9,
  input  a8,
  input  a7,
  input  a6,
  input  a5,
  input  a4,
  input  a3,
  input  a1,
  input  a0,
  input  a13,
  input  a11,
  input  a10,
  output sego
);

  wire or_1_out, or_2_out, or_3_out, or_4_out, or_5_out, or_6_out, or_7_out, or_8_out, or_9_out, or_10_out;

  or or_1 (or_1_out, a13, a11);
  or or_2 (or_2_out, a6, a5);
  or or_3 (or_3_out, or_1_out, a10);
  or or_4 (or_4_out, or_2_out, a9);
  or or_5 (or_5_out, or_4_out, a8);
  or or_6 (or_6_out, a4, a3);
  or or_7 (or_7_out, a1, or_8_out);
  or or_8 (or_8_out, a0, or_3_out);
  or or_9 (or_9_out, or_5_out, a7);
  or or_10 (or_10_out, or_6_out, or_7_out);
  or or_11 (sego, or_9_out, or_10_out);
endmodule

module Seg2_D (
  input  a9,
  input  a8,
  input  a6,
  input  a5,
  input  a3,
  input  a2,
  input  a0,
  input  a14,
  input  a13,
  input  a12,
  input  a11,
  output sego
);

  wire or_1_out, or_2_out, or_3_out, or_4_out, or_5_out, or_6_out, or_7_out, or_8_out, or_9_out;

  or or_1 (or_1_out, a14, a13);
  or or_2 (or_2_out, a12, a11);
  or or_3 (or_3_out, or_1_out, or_2_out);
  or or_4 (or_4_out, a9, a8);
  or or_5 (or_5_out, a5, a3);
  or or_6 (or_6_out, a2, or_7_out);
  or or_7 (or_7_out, a0, or_3_out);
  or or_8 (or_8_out, or_4_out, a6);
  or or_9 (or_9_out, or_5_out, or_6_out);
  or or_10 (sego, or_8_out, or_9_out);
endmodule

module Seg2_E (
  input  a8,
  input  a6,
  input  a2,
  input  a0,
  input  a15,
  input  a14,
  input  a13,
  input  a12,
  input  a11,
  input  a10,
  output sego
);

  wire or_1_out, or_2_out, or_3_out;

  or or_1 (or_1_out, a0, a15, a14, a13, a12, a11, a10);
  or or_2 (or_2_out, a8, a6);
  or or_3 (or_3_out, a2, or_1_out);
  or or_4 (sego, or_2_out, or_3_out);
endmodule

module Seg2_F (
  input  a8,
  input  a6,
  input  a5,
  input  a4,
  input  a2,
  input  a0,
  input  a9,
  input  a15,
  input  a14,
  input  a12,
  input  a11,
  input  a10,
  output sego
);

  wire or_1_out, or_2_out, or_3_out, or_4_out, or_5_out, or_6_out;

  or or_1 (or_1_out, a9, a0);
  or or_2 (or_2_out, a8, a6);
  or or_3 (or_3_out, a4, a2);
  or or_4 (or_4_out, or_1_out, a15, a14, a12, a11, a10);
  or or_5 (or_5_out, or_2_out, a5);
  or or_6 (or_6_out, or_3_out, or_4_out);
  or or_7 (sego, or_5_out, or_6_out);
endmodule

module Seg2_G (
  input  a8,
  input  a6,
  input  a5,
  input  a4,
  input  a3,
  input  a2,
  input  a9,
  input  a15,
  input  a14,
  input  a13,
  input  a11,
  input  a10,
  output sego
);

  wire or_1_out, or_2_out, or_3_out, or_4_out, or_5_out, or_6_out;

  or or_1 (or_1_out, a2, a9);
  or or_2 (or_2_out, or_1_out, a15, a14, a13, a11, a10);
  or or_3 (or_3_out, a8, a6);
  or or_4 (or_4_out, a3, or_2_out);
  or or_5 (or_5_out, or_3_out, a5);
  or or_6 (or_6_out, a4, or_4_out);
  or or_7 (sego, or_5_out, or_6_out);
endmodule

module Seg2_H (
  input  a15,
  input  a14,
  input  a13,
  input  a12,
  input  a11,
  input  a10,
  output sego
);

  wire or_1_out, or_2_out, or_3_out, or_4_out;

  or or_1 (or_1_out, a15, a14);
  or or_2 (or_2_out, a12, a11);
  or or_3 (or_3_out, or_1_out, a13);
  or or_4 (or_4_out, or_2_out, a10);
  or or_5 (sego, or_3_out, or_4_out);
endmodule

module abs_3bit (
  input  a3,
  input  a2,
  input  a1,
  input  a0,
  output y2,
  output y1,
  output y0
);

  wire not_1_out, not_2_out, not_3_out;

  not not_1 (not_1_out, a2);
  not not_2 (not_2_out, a1);
  not not_3 (not_3_out, a0);
  Multiplexer multiplexer_1 (.in0(a2), .in1(not_1_out), .out(y2), .sel(a3));
  Multiplexer multiplexer_2 (.in0(a1), .in1(not_2_out), .out(y1), .sel(a3));
  Multiplexer multiplexer_3 (.in0(a0), .in1(not_3_out), .out(y0), .sel(a3));
endmodule
