// Logisim project 1.2.d_sr-latch.circ as structural Verilog: 2 circuits, main circuit sr_latch
module sim (
  input  in_1,
  input  in_2,
  input  in_3
);

  wire and_1_out, and_2_out, sr_latch_1_q, sr_latch_1_qn;

  and and_1 (and_1_out, in_1, in_2);
  and and_2 (and_2_out, in_1, in_3);
  sr_latch sr_latch_1 (.R(and_1_out), .S(and_2_out), .Q(sr_latch_1_q), .Qn(sr_latch_1_qn));
  LED led_1 (.in(sr_latch_1_q));
  LED led_2 (.in(sr_latch_1_qn));
endmodule

module sr_latch (
  input  R,
  input  S,
  output Q,
  output Qn
);

  nor nor_1 (Q, R, Qn);
  nor nor_2 (Qn, Q, S);
endmodule
