// Logisim project 1.2.e_sr-latch2.circ as structural Verilog: 2 circuits, main circuit sr_latch2
module sim (
  input  in_1,
  input  in_2,
  input  in_3
);

  wire and_1_out, and_2_out, sr_latch2_1_q, sr_latch2_1_qn;

  and and_1 (and_1_out, in_1, in_2);
  and and_2 (and_2_out, in_1, in_3);
  sr_latch2 sr_latch2_1 (.Rn(and_1_out), .Sn(and_2_out), .Q(sr_latch2_1_q), .Qn(sr_latch2_1_qn));
  LED led_1 (.in(sr_latch2_1_q));
  LED led_2 (.in(sr_latch2_1_qn));
endmodule

module sr_latch2 (
  input  Rn,
  input  Sn,
  output Q,
  output Qn
);

  nand nand_1 (Q, Rn, Qn);
  nand nand_2 (Qn, Q, Sn);
endmodule
