// Logisim project 1.3.0_d-latch.circ as structural Verilog: 2 circuits, main circuit d_latch
module d_latch (
  input  D,
  input  WE,
  output Q
);

  wire and_1_out, and_2_out, not_1_out;

  not not_1 (not_1_out, D);
  and and_1 (and_1_out, D, WE);
  and and_2 (and_2_out, WE, not_1_out);
  sr_latch sr_latch_1 (.R(and_2_out), .S(and_1_out), .Q(Q));  // open: Qn
endmodule

module sr_latch (
  input  R,
  input  S,
  output Q,
  output Qn
);

  nor nor_1 (Q, R, Qn);
  nor nor_2 (Qn, Q, S);
endmodule
