// Logisim project 1.3.1_d-latch_rstn.circ as structural Verilog: 2 circuits, main circuit d_latch
module d_latch (
  input  D,
  input  WE,
  input  rstn,
  output Q
);

  wire and_1_out, and_2_out, not_1_out, sr_latch_1_q;

  not not_1 (not_1_out, D);
  and and_1 (and_1_out, D, WE);
  and and_2 (and_2_out, WE, not_1_out);
  sr_latch sr_latch_1 (.R(and_2_out), .S(and_1_out), .Q(sr_latch_1_q));  // open: Qn
  and and_3 (Q, rstn, sr_latch_1_q);
endmodule

module sr_latch (
  input  R,
  input  S,
  output Q,
  output Qn
);

  nor nor_1 (Q, R, Qn);
  nor nor_2 (Qn, Q, S);
endmodule
