// Logisim project 1.3.3_dff.circ as structural Verilog: 4 circuits, main circuit d_latch
module sim (
  input  in_1,
  output out_2
);

  wire button_1_out;

  Button button_1 (.out(button_1_out));
  dff dff_1 (.D(in_1), .CLK(button_1_out), .Q(out_2));
endmodule

module dff (
  input  D,
  input  CLK,
  output Q
);

  wire d_latch_1_q, not_1_out;

  not not_1 (not_1_out, CLK);
  d_latch d_latch_1 (.D(D), .WE(not_1_out), .Q(d_latch_1_q));
  d_latch d_latch_2 (.D(d_latch_1_q), .WE(CLK), .Q(Q));
endmodule

module d_latch (
  input  D,
  input  WE,
  output Q
);

  wire and_1_out, and_2_out, not_1_out;

  not not_1 (not_1_out, D);
  and and_1 (and_1_out, D, WE);
  and and_2 (and_2_out, WE, not_1_out);
  sr_latch sr_latch_1 (.R(and_2_out), .S(and_1_out), .Q(Q));  // open: Qn
endmodule

module sr_latch (
  input  R,
  input  S,
  output Q,
  output Qn
);

  nor nor_1 (Q, R, Qn);
  nor nor_2 (Qn, Q, S);
endmodule
