// Logisim project 1.3.5_dff_rstn_inv.circ as structural Verilog: 4 circuits, main circuit d_latch_rstn
module sim (
  input  in_1,
  output out_2
);

  wire button_1_out, not_1_out;

  Button button_1 (.out(button_1_out));
  not not_1 (not_1_out, out_2);
  dff_rstn dff_rstn_1 (.D(not_1_out), .CLK(button_1_out), .rstn(in_1), .Q(out_2));
endmodule

module dff_rstn (
  input  D,
  input  CLK,
  input  rstn,
  output Q
);

  wire d_latch_rstn_1_q, not_1_out;

  not not_1 (not_1_out, CLK);
  d_latch_rstn d_latch_rstn_1 (.D(D), .WE(not_1_out), .rstn(rstn), .Q(d_latch_rstn_1_q));
  d_latch_rstn d_latch_rstn_2 (.D(d_latch_rstn_1_q), .WE(CLK), .rstn(rstn), .Q(Q));
endmodule

module d_latch_rstn (
  input  D,
  input  WE,
  input  rstn,
  output Q
);

  wire and_1_out, and_2_out, and_3_out, not_1_out, not_2_out, or_1_out;

  not not_1 (not_1_out, D);
  and and_1 (and_1_out, D, WE);
  and and_2 (and_2_out, WE, not_1_out);
  not not_2 (not_2_out, rstn);
  or or_1 (or_1_out, and_2_out, not_2_out);
  and and_3 (and_3_out, and_1_out, rstn);
  sr_latch sr_latch_1 (.R(or_1_out), .S(and_3_out), .Q(Q));  // open: Qn
endmodule

module sr_latch (
  input  R,
  input  S,
  output Q,
  output Qn
);

  nor nor_1 (Q, R, Qn);
  nor nor_2 (Qn, Q, S);
endmodule
