// Logisim project 1.3.7_dffe_rstn.circ as structural Verilog: 4 circuits, main circuit d_latch_rstn
module sim (
  input  in_1,
  input  in_2,
  input  in_3,
  output out_4
);

  wire button_1_out;

  Button button_1 (.out(button_1_out));
  dff_rstn dff_rstn_1 (.D(in_1), .CLK(button_1_out), .EN(in_2), .rstn(in_3), .Q(out_4));
endmodule

module dff_rstn (
  input  D,
  input  CLK,
  input  EN,
  input  rstn,
  output Q
);

  wire and_1_out, d_latch_rstn_1_q, not_1_out;

  and and_1 (and_1_out, CLK, EN);
  not not_1 (not_1_out, and_1_out);
  d_latch_rstn d_latch_rstn_1 (.D(D), .WE(not_1_out), .rstn(rstn), .Q(d_latch_rstn_1_q));
  d_latch_rstn d_latch_rstn_2 (.D(d_latch_rstn_1_q), .WE(and_1_out), .rstn(rstn), .Q(Q));
endmodule

module d_latch_rstn (
  input  D,
  input  WE,
  input  rstn,
  output Q
);

  wire and_1_out, and_2_out, and_3_out, not_1_out, not_2_out, or_1_out;

  not not_1 (not_1_out, D);
  and and_1 (and_1_out, D, WE);
  and and_2 (and_2_out, WE, not_1_out);
  not not_2 (not_2_out, rstn);
  or or_1 (or_1_out, and_2_out, not_2_out);
  and and_3 (and_3_out, and_1_out, rstn);
  sr_latch sr_latch_1 (.R(or_1_out), .S(and_3_out), .Q(Q));  // open: Qn
endmodule

module sr_latch (
  input  R,
  input  S,
  output Q,
  output Qn
);

  nor nor_1 (Q, R, Qn);
  nor nor_2 (Qn, Q, S);
endmodule
