// Logisim project 1.3.9_cnt_4bit.circ as structural Verilog: 6 circuits, main circuit d_latch_rstn
module sim (
  input  rstn
);

  wire button_1_out, cnt_4bit_1_q0, cnt_4bit_1_q1, cnt_4bit_1_q2, cnt_4bit_1_q3, segctl_0tof_1_sega,
       segctl_0tof_1_segb, segctl_0tof_1_segc, segctl_0tof_1_segd, segctl_0tof_1_sege, segctl_0tof_1_segf,
       segctl_0tof_1_segg;

  Button button_1 (.out(button_1_out));
  cnt_4bit cnt_4bit_1 (
    .rstn(rstn), .clk(button_1_out), .q3(cnt_4bit_1_q3), .q2(cnt_4bit_1_q2), .q1(cnt_4bit_1_q1),
    .q0(cnt_4bit_1_q0));
  SegCtl_0tof segctl_0tof_1 (
    .a3(cnt_4bit_1_q3), .a2(cnt_4bit_1_q2), .a1(cnt_4bit_1_q1), .a0(cnt_4bit_1_q0),
    .segA(segctl_0tof_1_sega), .segB(segctl_0tof_1_segb), .segC(segctl_0tof_1_segc),
    .segD(segctl_0tof_1_segd), .segE(segctl_0tof_1_sege), .segF(segctl_0tof_1_segf), .segG(segctl_0tof_1_segg));
  _7_Segment_Display u_7_segment_display_1 (
    .g(segctl_0tof_1_segg), .f(segctl_0tof_1_segf), .a(segctl_0tof_1_sega), .b(segctl_0tof_1_segb),
    .e(segctl_0tof_1_sege), .d(segctl_0tof_1_segd), .c(segctl_0tof_1_segc));  // open: dp
endmodule

module cnt_4bit (
  input  rstn,
  input  clk,
  output q3,
  output q2,
  output q1,
  output q0
);

  wire x_full_adder_4bit_1_s0, x_full_adder_4bit_1_s1, x_full_adder_4bit_1_s2, x_full_adder_4bit_1_s3;

  x_full_adder_4bit x_full_adder_4bit_1 (
    .a3(q3), .a2(q2), .a1(q1), .a0(q0), .b3(1'b0), .b2(1'b0), .b1(1'b0), .b0(1'b1), .cin(1'b0),
    .s3(x_full_adder_4bit_1_s3), .s2(x_full_adder_4bit_1_s2), .s1(x_full_adder_4bit_1_s1),
    .s0(x_full_adder_4bit_1_s0));  // open: cout
  dff_rstn_4bit dff_rstn_4bit_1 (
    .D3(x_full_adder_4bit_1_s3), .D2(x_full_adder_4bit_1_s2), .D1(x_full_adder_4bit_1_s1),
    .D0(x_full_adder_4bit_1_s0), .RSTN(rstn), .CLK(clk), .Q3(q3), .Q2(q2), .Q1(q1), .Q0(q0));
endmodule

module dff_rstn_4bit (
  input  D3,
  input  D2,
  input  D1,
  input  D0,
  input  RSTN,
  input  CLK,
  output Q3,
  output Q2,
  output Q1,
  output Q0
);

  dff_rstn dff_rstn_1 (.D(D3), .CLK(CLK), .rstn(RSTN), .Q(Q3));
  dff_rstn dff_rstn_2 (.D(D2), .CLK(CLK), .rstn(RSTN), .Q(Q2));
  dff_rstn dff_rstn_3 (.D(D1), .CLK(CLK), .rstn(RSTN), .Q(Q1));
  dff_rstn dff_rstn_4 (.D(D0), .CLK(CLK), .rstn(RSTN), .Q(Q0));
endmodule

module dff_rstn (
  input  D,
  input  CLK,
  input  rstn,
  output Q
);

  wire d_latch_rstn_1_q, not_1_out;

  not not_1 (not_1_out, CLK);
  d_latch_rstn d_latch_rstn_1 (.D(D), .WE(not_1_out), .rstn(rstn), .Q(d_latch_rstn_1_q));
  d_latch_rstn d_latch_rstn_2 (.D(d_latch_rstn_1_q), .WE(CLK), .rstn(rstn), .Q(Q));
endmodule

module d_latch_rstn (
  input  D,
  input  WE,
  input  rstn,
  output Q
);

  wire and_1_out, and_2_out, and_3_out, not_1_out, not_2_out, or_1_out;

  not not_1 (not_1_out, D);
  and and_1 (and_1_out, D, WE);
  and and_2 (and_2_out, WE, not_1_out);
  not not_2 (not_2_out, rstn);
  or or_1 (or_1_out, and_2_out, not_2_out);
  and and_3 (and_3_out, and_1_out, rstn);
  sr_latch sr_latch_1 (.R(or_1_out), .S(and_3_out), .Q(Q));  // open: Qn
endmodule

module sr_latch (
  input  R,
  input  S,
  output Q,
  output Qn
);

  nor nor_1 (Q, R, Qn);
  nor nor_2 (Qn, Q, S);
endmodule
