// Logisim project 1.3.a_sum_1to10.circ as structural Verilog: 8 circuits, main circuit d_latch_rstn
module sum_1to10 (
  input  in_1
);

  wire button_1_out, cnt_4bit_1_q0, cnt_4bit_1_q1, cnt_4bit_1_q2, cnt_4bit_1_q3, dff_rstn_8bit_1_q0,
       dff_rstn_8bit_1_q1, dff_rstn_8bit_1_q2, dff_rstn_8bit_1_q3, dff_rstn_8bit_1_q4, dff_rstn_8bit_1_q5,
       dff_rstn_8bit_1_q6, dff_rstn_8bit_1_q7, full_adder_8bit_1_s0, full_adder_8bit_1_s1,
       full_adder_8bit_1_s2, full_adder_8bit_1_s3, full_adder_8bit_1_s4, full_adder_8bit_1_s5,
       full_adder_8bit_1_s6, full_adder_8bit_1_s7, nand_1_out, not_1_out, segctl_0tof_1_sega,
       segctl_0tof_1_segb, segctl_0tof_1_segc, segctl_0tof_1_segd, segctl_0tof_1_sege, segctl_0tof_1_segf,
       segctl_0tof_1_segg, segctl_0tof_2_sega, segctl_0tof_2_segb, segctl_0tof_2_segc, segctl_0tof_2_segd,
       segctl_0tof_2_sege, segctl_0tof_2_segf, segctl_0tof_2_segg;

  Button button_1 (.out(button_1_out));
  dff_rstn_8bit dff_rstn_8bit_1 (
    .D7(full_adder_8bit_1_s7), .D6(full_adder_8bit_1_s6), .D5(full_adder_8bit_1_s5),
    .D4(full_adder_8bit_1_s4), .D3(full_adder_8bit_1_s3), .D2(full_adder_8bit_1_s2),
    .D1(full_adder_8bit_1_s1), .D0(full_adder_8bit_1_s0), .RSTN(in_1), .CLK(button_1_out), .EN(nand_1_out),
    .Q7(dff_rstn_8bit_1_q7), .Q6(dff_rstn_8bit_1_q6), .Q5(dff_rstn_8bit_1_q5), .Q4(dff_rstn_8bit_1_q4),
    .Q3(dff_rstn_8bit_1_q3), .Q2(dff_rstn_8bit_1_q2), .Q1(dff_rstn_8bit_1_q1), .Q0(dff_rstn_8bit_1_q0));
  cnt_4bit cnt_4bit_1 (
    .rstn(in_1), .clk(button_1_out), .en(nand_1_out), .q3(cnt_4bit_1_q3), .q2(cnt_4bit_1_q2),
    .q1(cnt_4bit_1_q1), .q0(cnt_4bit_1_q0));
  nand nand_1 (nand_1_out, cnt_4bit_1_q3, ~cnt_4bit_1_q2, cnt_4bit_1_q1, ~cnt_4bit_1_q0);  // NAND_Gate
  not not_1 (not_1_out, nand_1_out);
  full_adder_8bit full_adder_8bit_1 (
    .a7(dff_rstn_8bit_1_q7), .a6(dff_rstn_8bit_1_q6), .a5(dff_rstn_8bit_1_q5), .a4(dff_rstn_8bit_1_q4),
    .a3(dff_rstn_8bit_1_q3), .a2(dff_rstn_8bit_1_q2), .a1(dff_rstn_8bit_1_q1), .a0(dff_rstn_8bit_1_q0),
    .b7(1'b0), .b6(1'b0), .b5(1'b0), .b4(1'b0), .b3(cnt_4bit_1_q3), .b2(cnt_4bit_1_q2), .b1(cnt_4bit_1_q1),
    .b0(cnt_4bit_1_q0), .s7(full_adder_8bit_1_s7), .s6(full_adder_8bit_1_s6), .s5(full_adder_8bit_1_s5),
    .s4(full_adder_8bit_1_s4), .s3(full_adder_8bit_1_s3), .s2(full_adder_8bit_1_s2),
    .s1(full_adder_8bit_1_s1), .s0(full_adder_8bit_1_s0));  // open: cout
  SegCtl_0tof segctl_0tof_1 (
    .a3(full_adder_8bit_1_s3), .a2(full_adder_8bit_1_s2), .a1(full_adder_8bit_1_s1),
    .a0(full_adder_8bit_1_s0), .segA(segctl_0tof_1_sega), .segB(segctl_0tof_1_segb),
    .segC(segctl_0tof_1_segc), .segD(segctl_0tof_1_segd), .segE(segctl_0tof_1_sege),
    .segF(segctl_0tof_1_segf), .segG(segctl_0tof_1_segg));
  SegCtl_0tof segctl_0tof_2 (
    .a3(full_adder_8bit_1_s7), .a2(full_adder_8bit_1_s6), .a1(full_adder_8bit_1_s5),
    .a0(full_adder_8bit_1_s4), .segA(segctl_0tof_2_sega), .segB(segctl_0tof_2_segb),
    .segC(segctl_0tof_2_segc), .segD(segctl_0tof_2_segd), .segE(segctl_0tof_2_sege),
    .segF(segctl_0tof_2_segf), .segG(segctl_0tof_2_segg));
  _7_Segment_Display u_7_segment_display_1 (
    .g(segctl_0tof_2_segg), .f(segctl_0tof_2_segf), .a(segctl_0tof_2_sega), .b(segctl_0tof_2_segb),
    .e(segctl_0tof_2_sege), .d(segctl_0tof_2_segd), .c(segctl_0tof_2_segc));  // open: dp
  LED led_1 (.in(not_1_out));
  _7_Segment_Display u_7_segment_display_2 (
    .g(segctl_0tof_1_segg), .f(segctl_0tof_1_segf), .a(segctl_0tof_1_sega), .b(segctl_0tof_1_segb),
    .e(segctl_0tof_1_sege), .d(segctl_0tof_1_segd), .c(segctl_0tof_1_segc));  // open: dp
endmodule

module cnt_4bit (
  input  rstn,
  input  clk,
  input  en,
  output q3,
  output q2,
  output q1,
  output q0
);

  wire x_full_adder_4bit_1_s0, x_full_adder_4bit_1_s1, x_full_adder_4bit_1_s2, x_full_adder_4bit_1_s3;

  x_full_adder_4bit x_full_adder_4bit_1 (
    .a3(q3), .a2(q2), .a1(q1), .a0(q0), .b3(1'b0), .b2(1'b0), .b1(1'b0), .b0(1'b1), .cin(1'b0),
    .s3(x_full_adder_4bit_1_s3), .s2(x_full_adder_4bit_1_s2), .s1(x_full_adder_4bit_1_s1),
    .s0(x_full_adder_4bit_1_s0));  // open: cout
  dff_rstn_4bit dff_rstn_4bit_1 (
    .D3(x_full_adder_4bit_1_s3), .D2(x_full_adder_4bit_1_s2), .D1(x_full_adder_4bit_1_s1),
    .D0(x_full_adder_4bit_1_s0), .RSTN(rstn), .CLK(clk), .EN(en), .Q3(q3), .Q2(q2), .Q1(q1), .Q0(q0));
endmodule

module full_adder_8bit (
  input  a7,
  input  a6,
  input  a5,
  input  a4,
  input  a3,
  input  a2,
  input  a1,
  input  a0,
  input  b7,
  input  b6,
  input  b5,
  input  b4,
  input  b3,
  input  b2,
  input  b1,
  input  b0,
  output s7,
  output s6,
  output s5,
  output s4,
  output s3,
  output s2,
  output s1,
  output s0,
  output cout
);

  wire x_full_adder_4bit_2_cout;

  x_full_adder_4bit x_full_adder_4bit_1 (
    .a3(a7), .a2(a6), .a1(a5), .a0(a4), .b3(b7), .b2(b6), .b1(b5), .b0(b4), .cin(x_full_adder_4bit_2_cout),
    .s3(s7), .s2(s6), .s1(s5), .s0(s4), .cout(cout));
  x_full_adder_4bit x_full_adder_4bit_2 (
    .a3(a3), .a2(a2), .a1(a1), .a0(a0), .b3(b3), .b2(b2), .b1(b1), .b0(b0), .cin(1'b0), .s3(s3), .s2(s2),
    .s1(s1), .s0(s0), .cout(x_full_adder_4bit_2_cout));
endmodule

module dff_rstn_8bit (
  input  D7,
  input  D6,
  input  D5,
  input  D4,
  input  D3,
  input  D2,
  input  D1,
  input  D0,
  input  RSTN,
  input  CLK,
  input  EN,
  output Q7,
  output Q6,
  output Q5,
  output Q4,
  output Q3,
  output Q2,
  output Q1,
  output Q0
);

  dff_rstn_4bit dff_rstn_4bit_1 (
    .D3(D7), .D2(D6), .D1(D5), .D0(D4), .RSTN(RSTN), .CLK(CLK), .EN(EN), .Q3(Q7), .Q2(Q6), .Q1(Q5), .Q0(Q4));
  dff_rstn_4bit dff_rstn_4bit_2 (
    .D3(D3), .D2(D2), .D1(D1), .D0(D0), .RSTN(RSTN), .CLK(CLK), .EN(EN), .Q3(Q3), .Q2(Q2), .Q1(Q1), .Q0(Q0));
endmodule

module dff_rstn_4bit (
  input  D3,
  input  D2,
  input  D1,
  input  D0,
  input  RSTN,
  input  CLK,
  input  EN,
  output Q3,
  output Q2,
  output Q1,
  output Q0
);

  dff_rstn dff_rstn_1 (.D(D3), .CLK(CLK), .rstn(RSTN), .EN(EN), .Q(Q3));
  dff_rstn dff_rstn_2 (.D(D2), .CLK(CLK), .rstn(RSTN), .EN(EN), .Q(Q2));
  dff_rstn dff_rstn_3 (.D(D1), .CLK(CLK), .rstn(RSTN), .EN(EN), .Q(Q1));
  dff_rstn dff_rstn_4 (.D(D0), .CLK(CLK), .rstn(RSTN), .EN(EN), .Q(Q0));
endmodule

module dff_rstn (
  input  D,
  input  CLK,
  input  rstn,
  input  EN,
  output Q
);

  wire and_1_out, d_latch_rstn_1_q, not_1_out;

  and and_1 (and_1_out, CLK, EN);
  not not_1 (not_1_out, and_1_out);
  d_latch_rstn d_latch_rstn_1 (.D(D), .WE(not_1_out), .rstn(rstn), .Q(d_latch_rstn_1_q));
  d_latch_rstn d_latch_rstn_2 (.D(d_latch_rstn_1_q), .WE(and_1_out), .rstn(rstn), .Q(Q));
endmodule

module d_latch_rstn (
  input  D,
  input  WE,
  input  rstn,
  output Q
);

  wire and_1_out, and_2_out, and_3_out, not_1_out, not_2_out, or_1_out;

  not not_1 (not_1_out, D);
  and and_1 (and_1_out, D, WE);
  and and_2 (and_2_out, WE, not_1_out);
  not not_2 (not_2_out, rstn);
  or or_1 (or_1_out, and_2_out, not_2_out);
  and and_3 (and_3_out, and_1_out, rstn);
  sr_latch sr_latch_1 (.R(or_1_out), .S(and_3_out), .Q(Q));  // open: Qn
endmodule

module sr_latch (
  input  R,
  input  S,
  output Q,
  output Qn
);

  nor nor_1 (Q, R, Qn);
  nor nor_2 (Qn, Q, S);
endmodule
