// Logisim project 1.3.b_elec_clock.circ as structural Verilog: 9 circuits, main circuit elec_clock
module elec_clock (
  input  rstn,
  input  in_2
);

  wire and_1_out, and_2_out, and_3_out, and_4_out, and_5_out, and_6_out, and_7_out, button_1_out,
       clock_1_out, cnt_4bit_1_q0, cnt_4bit_1_q1, cnt_4bit_1_q2, cnt_4bit_1_q3, multiplexer_1_out,
       seg1_ctl_q0, seg1_ctl_q1, seg1_ctl_q2, seg1_ctl_q3, seg2_ctl_q0, seg2_ctl_q1, seg2_ctl_q2,
       seg2_ctl_q3, seg3_ctl_q0, seg3_ctl_q1, seg3_ctl_q2, seg3_ctl_q3, segctl_0tof_1_sega,
       segctl_0tof_1_segb, segctl_0tof_1_segc, segctl_0tof_1_segd, segctl_0tof_1_sege, segctl_0tof_1_segf,
       segctl_0tof_1_segg, segctl_0tof_2_sega, segctl_0tof_2_segb, segctl_0tof_2_segc, segctl_0tof_2_segd,
       segctl_0tof_2_sege, segctl_0tof_2_segf, segctl_0tof_2_segg, segctl_0tof_3_sega, segctl_0tof_3_segb,
       segctl_0tof_3_segc, segctl_0tof_3_segd, segctl_0tof_3_sege, segctl_0tof_3_segf, segctl_0tof_3_segg,
       segctl_0tof_4_sega, segctl_0tof_4_segb, segctl_0tof_4_segc, segctl_0tof_4_segd, segctl_0tof_4_sege,
       segctl_0tof_4_segf, segctl_0tof_4_segg;

  Clock clock_1 (.out(clock_1_out));
  Button button_1 (.out(button_1_out));
  Multiplexer multiplexer_1 (.in0(clock_1_out), .in1(button_1_out), .out(multiplexer_1_out), .sel(in_2));
  and and_1 (and_1_out, and_7_out, and_3_out);
  and and_2 (and_2_out, and_1_out, and_4_out);
  cnt_4bit cnt_4bit_1 (
    .rstn(rstn), .clk(multiplexer_1_out), .en(1'b1), .clr(and_5_out), .q3(cnt_4bit_1_q3), .q2(cnt_4bit_1_q2),
    .q1(cnt_4bit_1_q1), .q0(cnt_4bit_1_q0));
  cnt_4bit2 seg1_ctl (
    .rstn(rstn), .clk(multiplexer_1_out), .en(and_5_out), .clr(and_7_out), .q3(seg1_ctl_q3),
    .q2(seg1_ctl_q2), .q1(seg1_ctl_q1), .q0(seg1_ctl_q0));
  cnt_4bit2 seg2_ctl (
    .rstn(rstn), .clk(multiplexer_1_out), .en(and_7_out), .clr(and_1_out), .q3(seg2_ctl_q3),
    .q2(seg2_ctl_q2), .q1(seg2_ctl_q1), .q0(seg2_ctl_q0));
  cnt_4bit2 seg3_ctl (
    .rstn(rstn), .clk(multiplexer_1_out), .en(and_1_out), .clr(and_2_out), .q3(seg3_ctl_q3),
    .q2(seg3_ctl_q2), .q1(seg3_ctl_q1), .q0(seg3_ctl_q0));
  and and_3 (and_3_out, seg2_ctl_q3, ~seg2_ctl_q2, ~seg2_ctl_q1, seg2_ctl_q0);  // AND_Gate
  and and_4 (and_4_out, ~seg3_ctl_q3, seg3_ctl_q2, ~seg3_ctl_q1, seg3_ctl_q0);  // AND_Gate
  and and_5 (and_5_out, cnt_4bit_1_q3, ~cnt_4bit_1_q2, ~cnt_4bit_1_q1, cnt_4bit_1_q0);  // AND_Gate
  and and_6 (and_6_out, ~seg1_ctl_q3, seg1_ctl_q2, ~seg1_ctl_q1, seg1_ctl_q0);  // AND_Gate
  and and_7 (and_7_out, and_6_out, and_5_out);
  SegCtl_0tof segctl_0tof_1 (
    .a3(seg2_ctl_q3), .a2(seg2_ctl_q2), .a1(seg2_ctl_q1), .a0(seg2_ctl_q0), .segA(segctl_0tof_1_sega),
    .segB(segctl_0tof_1_segb), .segC(segctl_0tof_1_segc), .segD(segctl_0tof_1_segd),
    .segE(segctl_0tof_1_sege), .segF(segctl_0tof_1_segf), .segG(segctl_0tof_1_segg));
  SegCtl_0tof segctl_0tof_2 (
    .a3(seg3_ctl_q3), .a2(seg3_ctl_q2), .a1(seg3_ctl_q1), .a0(seg3_ctl_q0), .segA(segctl_0tof_2_sega),
    .segB(segctl_0tof_2_segb), .segC(segctl_0tof_2_segc), .segD(segctl_0tof_2_segd),
    .segE(segctl_0tof_2_sege), .segF(segctl_0tof_2_segf), .segG(segctl_0tof_2_segg));
  _7_Segment_Display u_7_segment_display_1 (
    .g(segctl_0tof_2_segg), .f(segctl_0tof_2_segf), .a(segctl_0tof_2_sega), .b(segctl_0tof_2_segb),
    .e(segctl_0tof_2_sege), .d(segctl_0tof_2_segd), .c(segctl_0tof_2_segc));  // open: dp
  _7_Segment_Display u_7_segment_display_2 (
    .g(segctl_0tof_1_segg), .f(segctl_0tof_1_segf), .a(segctl_0tof_1_sega), .b(segctl_0tof_1_segb),
    .e(segctl_0tof_1_sege), .d(segctl_0tof_1_segd), .c(segctl_0tof_1_segc));  // open: dp
  SegCtl_0tof segctl_0tof_3 (
    .a3(cnt_4bit_1_q3), .a2(cnt_4bit_1_q2), .a1(cnt_4bit_1_q1), .a0(cnt_4bit_1_q0),
    .segA(segctl_0tof_3_sega), .segB(segctl_0tof_3_segb), .segC(segctl_0tof_3_segc),
    .segD(segctl_0tof_3_segd), .segE(segctl_0tof_3_sege), .segF(segctl_0tof_3_segf), .segG(segctl_0tof_3_segg));
  SegCtl_0tof segctl_0tof_4 (
    .a3(seg1_ctl_q3), .a2(seg1_ctl_q2), .a1(seg1_ctl_q1), .a0(seg1_ctl_q0), .segA(segctl_0tof_4_sega),
    .segB(segctl_0tof_4_segb), .segC(segctl_0tof_4_segc), .segD(segctl_0tof_4_segd),
    .segE(segctl_0tof_4_sege), .segF(segctl_0tof_4_segf), .segG(segctl_0tof_4_segg));
  _7_Segment_Display u_7_segment_display_3 (
    .g(segctl_0tof_4_segg), .f(segctl_0tof_4_segf), .a(segctl_0tof_4_sega), .b(segctl_0tof_4_segb),
    .e(segctl_0tof_4_sege), .d(segctl_0tof_4_segd), .c(segctl_0tof_4_segc));  // open: dp
  _7_Segment_Display u_7_segment_display_4 (
    .g(segctl_0tof_3_segg), .f(segctl_0tof_3_segf), .a(segctl_0tof_3_sega), .b(segctl_0tof_3_segb),
    .e(segctl_0tof_3_sege), .d(segctl_0tof_3_segd), .c(segctl_0tof_3_segc));  // open: dp

  // Notes on the sheet:
  //   seg0_ctl
  //   seg3
  //   seg2
  //   seg1
  //   seg0
endmodule

module cnt_4bit (
  input  rstn,
  input  clk,
  input  en,
  input  clr,
  output q3,
  output q2,
  output q1,
  output q0
);

  wire x_full_adder_4bit_1_s0, x_full_adder_4bit_1_s1, x_full_adder_4bit_1_s2, x_full_adder_4bit_1_s3;

  x_full_adder_4bit x_full_adder_4bit_1 (
    .a3(q3), .a2(q2), .a1(q1), .a0(q0), .b3(1'b0), .b2(1'b0), .b1(1'b0), .b0(1'b1), .cin(1'b0),
    .s3(x_full_adder_4bit_1_s3), .s2(x_full_adder_4bit_1_s2), .s1(x_full_adder_4bit_1_s1),
    .s0(x_full_adder_4bit_1_s0));  // open: cout
  dff_rstn_4bit dff_rstn_4bit_1 (
    .D3(x_full_adder_4bit_1_s3), .D2(x_full_adder_4bit_1_s2), .D1(x_full_adder_4bit_1_s1),
    .D0(x_full_adder_4bit_1_s0), .RSTN(rstn), .CLK(clk), .EN(en), .CLR(clr), .Q3(q3), .Q2(q2), .Q1(q1),
    .Q0(q0));
endmodule

module cnt_4bit2 (
  input  rstn,
  input  clk,
  input  en,
  input  clr,
  output q3,
  output q2,
  output q1,
  output q0
);

  wire x_full_adder_4bit_1_s0, x_full_adder_4bit_1_s1, x_full_adder_4bit_1_s2, x_full_adder_4bit_1_s3;

  x_full_adder_4bit x_full_adder_4bit_1 (
    .a3(q3), .a2(q2), .a1(q1), .a0(q0), .b3(1'b0), .b2(1'b0), .b1(1'b0), .b0(en), .cin(1'b0),
    .s3(x_full_adder_4bit_1_s3), .s2(x_full_adder_4bit_1_s2), .s1(x_full_adder_4bit_1_s1),
    .s0(x_full_adder_4bit_1_s0));  // open: cout
  dff_rstn_4bit dff_rstn_4bit_1 (
    .D3(x_full_adder_4bit_1_s3), .D2(x_full_adder_4bit_1_s2), .D1(x_full_adder_4bit_1_s1),
    .D0(x_full_adder_4bit_1_s0), .RSTN(rstn), .CLK(clk), .EN(1'b1), .CLR(clr), .Q3(q3), .Q2(q2), .Q1(q1),
    .Q0(q0));
endmodule

module full_adder_8bit (
  input  a7,
  input  a6,
  input  a5,
  input  a4,
  input  a3,
  input  a2,
  input  a1,
  input  a0,
  input  b7,
  input  b6,
  input  b5,
  input  b4,
  input  b3,
  input  b2,
  input  b1,
  input  b0,
  output s7,
  output s6,
  output s5,
  output s4,
  output s3,
  output s2,
  output s1,
  output s0,
  output cout
);

  wire x_full_adder_4bit_2_cout;

  x_full_adder_4bit x_full_adder_4bit_1 (
    .a3(a7), .a2(a6), .a1(a5), .a0(a4), .b3(b7), .b2(b6), .b1(b5), .b0(b4), .cin(x_full_adder_4bit_2_cout),
    .s3(s7), .s2(s6), .s1(s5), .s0(s4), .cout(cout));
  x_full_adder_4bit x_full_adder_4bit_2 (
    .a3(a3), .a2(a2), .a1(a1), .a0(a0), .b3(b3), .b2(b2), .b1(b1), .b0(b0), .cin(1'b0), .s3(s3), .s2(s2),
    .s1(s1), .s0(s0), .cout(x_full_adder_4bit_2_cout));
endmodule

module dff_rstn_8bit (
  input  D7,
  input  D6,
  input  D5,
  input  D4,
  input  D3,
  input  D2,
  input  D1,
  input  D0,
  input  RSTN,
  input  CLK,
  input  EN,
  input  CLR,
  output Q7,
  output Q6,
  output Q5,
  output Q4,
  output Q3,
  output Q2,
  output Q1,
  output Q0
);

  dff_rstn_4bit dff_rstn_4bit_1 (
    .D3(D7), .D2(D6), .D1(D5), .D0(D4), .RSTN(RSTN), .CLK(CLK), .EN(EN), .CLR(CLR), .Q3(Q7), .Q2(Q6),
    .Q1(Q5), .Q0(Q4));
  dff_rstn_4bit dff_rstn_4bit_2 (
    .D3(D3), .D2(D2), .D1(D1), .D0(D0), .RSTN(RSTN), .CLK(CLK), .EN(EN), .CLR(CLR), .Q3(Q3), .Q2(Q2),
    .Q1(Q1), .Q0(Q0));
endmodule

module dff_rstn_4bit (
  input  D3,
  input  D2,
  input  D1,
  input  D0,
  input  RSTN,
  input  CLK,
  input  EN,
  input  CLR,
  output Q3,
  output Q2,
  output Q1,
  output Q0
);

  dff_rstn dff_rstn_1 (.D(D3), .CLK(CLK), .rstn(RSTN), .EN(EN), .CLR(CLR), .Q(Q3));
  dff_rstn dff_rstn_2 (.D(D2), .CLK(CLK), .rstn(RSTN), .EN(EN), .CLR(CLR), .Q(Q2));
  dff_rstn dff_rstn_3 (.D(D1), .CLK(CLK), .rstn(RSTN), .EN(EN), .CLR(CLR), .Q(Q1));
  dff_rstn dff_rstn_4 (.D(D0), .CLK(CLK), .rstn(RSTN), .EN(EN), .CLR(CLR), .Q(Q0));
endmodule

module dff_rstn (
  input  D,
  input  CLK,
  input  rstn,
  input  EN,
  input  CLR,
  output Q
);

  wire and_1_out, and_2_out, d_latch_rstn_1_q, not_1_out, not_2_out;

  not not_1 (not_1_out, CLR);
  and and_1 (and_1_out, CLK, EN);
  not not_2 (not_2_out, and_1_out);
  and and_2 (and_2_out, D, not_1_out);
  d_latch_rstn d_latch_rstn_1 (.D(and_2_out), .WE(not_2_out), .rstn(rstn), .Q(d_latch_rstn_1_q));
  d_latch_rstn d_latch_rstn_2 (.D(d_latch_rstn_1_q), .WE(and_1_out), .rstn(rstn), .Q(Q));
endmodule

module d_latch_rstn (
  input  D,
  input  WE,
  input  rstn,
  output Q
);

  wire and_1_out, and_2_out, and_3_out, not_1_out, not_2_out, or_1_out;

  not not_1 (not_1_out, D);
  and and_1 (and_1_out, D, WE);
  and and_2 (and_2_out, WE, not_1_out);
  not not_2 (not_2_out, rstn);
  or or_1 (or_1_out, and_2_out, not_2_out);
  and and_3 (and_3_out, and_1_out, rstn);
  sr_latch sr_latch_1 (.R(or_1_out), .S(and_3_out), .Q(Q));  // open: Qn
endmodule

module sr_latch (
  input  R,
  input  S,
  output Q,
  output Qn
);

  nor nor_1 (Q, R, Qn);
  nor nor_2 (Qn, Q, S);
endmodule
