// Logisim project F5_1.3.1_sCPU.circ as structural Verilog: 7 circuits, main circuit sCPU_li
module sCPU_li (
  input  rstn
);

  wire and_1_out, clock_1_out, comparator_1_eq, decoder_2to4_1_y0, decoder_2to4_1_y1, decoder_2to4_1_y2,
       decoder_2to4_1_y3, not_1_out, or_1_out, or_2_out, segctl_0tof_1_sega, segctl_0tof_1_segb,
       segctl_0tof_1_segc, segctl_0tof_1_segd, segctl_0tof_1_sege, segctl_0tof_1_segf, segctl_0tof_1_segg,
       segctl_0tof_2_sega, segctl_0tof_2_segb, segctl_0tof_2_segc, segctl_0tof_2_segd, segctl_0tof_2_sege,
       segctl_0tof_2_segf, segctl_0tof_2_segg;
  wire [1:0] multiplexer_3_out;
  wire [3:0] add1_1_add1_out, multiplexer_1_out, pc_1_q;
  wire [7:0] alu_1_alu_o, dff_8bit_1_q, multiplexer_2_out, ram_4x8_1_rdata1, ram_4x8_1_rdata2,
       rom_16x8_1_rom_o;

  Clock clock_1 (.out(clock_1_out));
  rom_16x8 rom_16x8_1 (
    .rom0(8'h8a), .rom1(8'h90), .rom2(8'ha0), .rom3(8'hb1), .rom4(8'h17), .rom5(8'h29), .rom6(8'hd1),
    .rom7(8'h42), .rom8(8'he3), .addr(pc_1_q), .rom_o(rom_16x8_1_rom_o));  // open: rom9, rom10, rom11, rom12, rom13, rom14, rom15
  add1 add1_1 (.add1_in(pc_1_q), .add1_out(add1_1_add1_out));
  Multiplexer #(.width(4)) multiplexer_1 (
    .in0(rom_16x8_1_rom_o[5:2]), .in1(add1_1_add1_out), .out(multiplexer_1_out), .sel(or_2_out));
  pc pc_1 (.d(multiplexer_1_out), .rstn(rstn), .clk(clock_1_out), .q(pc_1_q));
  alu alu_1 (.in0(ram_4x8_1_rdata1), .in1(ram_4x8_1_rdata2), .alu_o(alu_1_alu_o));
  decoder_2to4 decoder_2to4_1 (
    .a1(rom_16x8_1_rom_o[7]), .a0(rom_16x8_1_rom_o[6]), .y3(decoder_2to4_1_y3), .y2(decoder_2to4_1_y2),
    .y1(decoder_2to4_1_y1), .y0(decoder_2to4_1_y0));
  or or_1 (or_1_out, decoder_2to4_1_y2, decoder_2to4_1_y0);
  Multiplexer #(.select(2), .width(8)) multiplexer_2 (
    .in0(alu_1_alu_o), .in1({8{1'b0}}), .in2({4'b0000, rom_16x8_1_rom_o[3:0]}), .in3({8{1'b0}}),
    .out(multiplexer_2_out), .sel(rom_16x8_1_rom_o[7:6]));
  dff_8bit dff_8bit_1 (
    .D(ram_4x8_1_rdata2), .RSTN(rstn), .CLK(clock_1_out), .EN(decoder_2to4_1_y1), .Q(dff_8bit_1_q));  // open: CLR
  Multiplexer #(.width(2)) multiplexer_3 (
    .in0(rom_16x8_1_rom_o[3:2]), .in1(2'b00), .out(multiplexer_3_out), .sel(decoder_2to4_1_y3));
  or or_2 (or_2_out, and_1_out, not_1_out);
  ram_4x8 ram_4x8_1 (
    .wdata(multiplexer_2_out), .rstn(rstn), .clk(clock_1_out), .wen(or_1_out), .waddr(rom_16x8_1_rom_o[5:4]),
    .raddr1(multiplexer_3_out), .raddr2(rom_16x8_1_rom_o[1:0]), .rdata1(ram_4x8_1_rdata1),
    .rdata2(ram_4x8_1_rdata2));
  Comparator #(.mode("unsigned")) comparator_1 (
    .a(ram_4x8_1_rdata1), .b(ram_4x8_1_rdata2), .eq(comparator_1_eq));  // open: gt, lt
  and and_1 (and_1_out, comparator_1_eq, decoder_2to4_1_y3);
  not not_1 (not_1_out, decoder_2to4_1_y3);
  SegCtl_0tof segctl_0tof_1 (
    .a3(dff_8bit_1_q[7]), .a2(dff_8bit_1_q[6]), .a1(dff_8bit_1_q[5]), .a0(dff_8bit_1_q[4]),
    .segA(segctl_0tof_1_sega), .segB(segctl_0tof_1_segb), .segC(segctl_0tof_1_segc),
    .segD(segctl_0tof_1_segd), .segE(segctl_0tof_1_sege), .segF(segctl_0tof_1_segf), .segG(segctl_0tof_1_segg));
  SegCtl_0tof segctl_0tof_2 (
    .a3(dff_8bit_1_q[3]), .a2(dff_8bit_1_q[2]), .a1(dff_8bit_1_q[1]), .a0(dff_8bit_1_q[0]),
    .segA(segctl_0tof_2_sega), .segB(segctl_0tof_2_segb), .segC(segctl_0tof_2_segc),
    .segD(segctl_0tof_2_segd), .segE(segctl_0tof_2_sege), .segF(segctl_0tof_2_segf), .segG(segctl_0tof_2_segg));
  _7_Segment_Display u_7_segment_display_1 (
    .g(segctl_0tof_1_segg), .f(segctl_0tof_1_segf), .a(segctl_0tof_1_sega), .b(segctl_0tof_1_segb),
    .e(segctl_0tof_1_sege), .d(segctl_0tof_1_segd), .c(segctl_0tof_1_segc));  // open: dp
  _7_Segment_Display u_7_segment_display_2 (
    .g(segctl_0tof_2_segg), .f(segctl_0tof_2_segf), .a(segctl_0tof_2_sega), .b(segctl_0tof_2_segb),
    .e(segctl_0tof_2_sege), .d(segctl_0tof_2_segd), .c(segctl_0tof_2_segc));  // open: dp

  // Notes on the sheet:
  //   benr0_addr
  //   opcode
  //   rd
  //   rs1
  //   rs2
  //   imm
endmodule

module rom_16x8 (
  input  [7:0] rom0,
  input  [7:0] rom1,
  input  [7:0] rom2,
  input  [7:0] rom3,
  input  [7:0] rom4,
  input  [7:0] rom5,
  input  [7:0] rom6,
  input  [7:0] rom7,
  input  [7:0] rom8,
  input  [7:0] rom9,
  input  [7:0] rom10,
  input  [7:0] rom11,
  input  [7:0] rom12,
  input  [7:0] rom13,
  input  [7:0] rom14,
  input  [7:0] rom15,
  input  [3:0] addr,
  output [7:0] rom_o
);

  Multiplexer #(.select(4), .width(8)) multiplexer_1 (
    .in0(rom0), .in1(rom1), .in2(rom2), .in3(rom3), .in4(rom4), .in5(rom5), .in6(rom6), .in7(rom7),
    .in8(rom8), .in9(rom9), .in10(rom10), .in11(rom11), .in12(rom12), .in13(rom13), .in14(rom14),
    .in15(rom15), .out(rom_o), .sel(addr));
endmodule

module ram_4x8 (
  input  [7:0] wdata,
  input  rstn,
  input  clk,
  input  wen,
  input  [1:0] waddr,
  input  [1:0] raddr1,
  input  [1:0] raddr2,
  output [7:0] rdata1,
  output [7:0] rdata2
);

  wire and_1_out, and_2_out, and_3_out, and_4_out, decoder_2to4_1_y0, decoder_2to4_1_y1, decoder_2to4_1_y2,
       decoder_2to4_1_y3;
  wire [7:0] ram0_q, ram1_q, ram2_q, ram3_q;

  decoder_2to4 decoder_2to4_1 (
    .a1(waddr[1]), .a0(waddr[0]), .y3(decoder_2to4_1_y3), .y2(decoder_2to4_1_y2), .y1(decoder_2to4_1_y1),
    .y0(decoder_2to4_1_y0));
  and and_1 (and_1_out, wen, decoder_2to4_1_y0);
  and and_2 (and_2_out, wen, decoder_2to4_1_y1);
  and and_3 (and_3_out, decoder_2to4_1_y2, wen);
  and and_4 (and_4_out, wen, decoder_2to4_1_y3);
  dff_8bit ram0 (.D(wdata), .RSTN(rstn), .CLK(clk), .EN(and_1_out), .CLR(1'b0), .Q(ram0_q));
  dff_8bit ram1 (.D(wdata), .RSTN(rstn), .CLK(clk), .EN(and_2_out), .CLR(1'b0), .Q(ram1_q));
  dff_8bit ram2 (.D(wdata), .RSTN(rstn), .CLK(clk), .EN(and_3_out), .CLR(1'b0), .Q(ram2_q));
  dff_8bit ram3 (.D(wdata), .RSTN(rstn), .CLK(clk), .EN(and_4_out), .CLR(1'b0), .Q(ram3_q));
  Multiplexer #(.select(2), .width(8)) multiplexer_1 (
    .in0(ram0_q), .in1(ram1_q), .in2(ram2_q), .in3(ram3_q), .out(rdata1), .sel(raddr1));
  Multiplexer #(.select(2), .width(8)) multiplexer_2 (
    .in0(ram0_q), .in1(ram1_q), .in2(ram2_q), .in3(ram3_q), .out(rdata2), .sel(raddr2));
endmodule

module pc (
  input  [3:0] d,
  input  rstn,
  input  clk,
  output [3:0] q
);

  dff_4bit dff_4bit_1 (
    .D3(d[3]), .D2(d[2]), .D1(d[1]), .D0(d[0]), .RSTN(rstn), .CLK(clk), .EN(1'b1), .CLR(1'b0), .Q3(q[3]),
    .Q2(q[2]), .Q1(q[1]), .Q0(q[0]));
endmodule

module add1 (
  input  [3:0] add1_in,
  output [3:0] add1_out
);

  x_full_adder_4bit x_full_adder_4bit_1 (
    .a3(add1_in[3]), .a2(add1_in[2]), .a1(add1_in[1]), .a0(add1_in[0]), .b3(1'b0), .b2(1'b0), .b1(1'b0),
    .b0(1'b1), .cin(1'b0), .s3(add1_out[3]), .s2(add1_out[2]), .s1(add1_out[1]), .s0(add1_out[0]));  // open: cout
endmodule

module alu (
  input  [7:0] in0,
  input  [7:0] in1,
  output [7:0] alu_o
);

  adder_8bit adder_8bit_1 (.add_in0(in0), .add_in1(in1), .add_o(alu_o));
endmodule

module adder_8bit (
  input  [7:0] add_in0,
  input  [7:0] add_in1,
  output [7:0] add_o
);

  wire x_full_adder_4bit_2_cout;

  x_full_adder_4bit x_full_adder_4bit_1 (
    .a3(add_in0[7]), .a2(add_in0[6]), .a1(add_in0[5]), .a0(add_in0[4]), .b3(add_in1[7]), .b2(add_in1[6]),
    .b1(add_in1[5]), .b0(add_in1[4]), .cin(x_full_adder_4bit_2_cout), .s3(add_o[7]), .s2(add_o[6]),
    .s1(add_o[5]), .s0(add_o[4]));  // open: cout
  x_full_adder_4bit x_full_adder_4bit_2 (
    .a3(add_in0[3]), .a2(add_in0[2]), .a1(add_in0[1]), .a0(add_in0[0]), .b3(add_in1[3]), .b2(add_in1[2]),
    .b1(add_in1[1]), .b0(add_in1[0]), .cin(1'b0), .s3(add_o[3]), .s2(add_o[2]), .s1(add_o[1]), .s0(add_o[0]),
    .cout(x_full_adder_4bit_2_cout));
endmodule
