// Logisim project F5_1.3.1_sCPU_li.circ as structural Verilog
module rom_16x8 (
  input  [7:0] rom0,
  input  [7:0] rom1,
  input  [7:0] rom2,
  input  [7:0] rom3,
  input  [7:0] rom4,
  input  [7:0] rom5,
  input  [7:0] rom6,
  input  [7:0] rom7,
  input  [7:0] rom8,
  input  [7:0] rom9,
  input  [7:0] rom10,
  input  [7:0] rom11,
  input  [7:0] rom12,
  input  [7:0] rom13,
  input  [7:0] rom14,
  input  [7:0] rom15,
  input  [3:0] addr,
  output [7:0] rom_o
);

  Multiplexer #(.select(4), .width(8)) multiplexer_1 (
    .in0(rom0), .in1(rom1), .in2(rom2), .in3(rom3), .in4(rom4), .in5(rom5), .in6(rom6), .in7(rom7),
    .in8(rom8), .in9(rom9), .in10(rom10), .in11(rom11), .in12(rom12), .in13(rom13), .in14(rom14),
    .in15(rom15), .out(rom_o), .sel(addr));
endmodule

module ram_4x8 (
  input  [7:0] data,
  input  rstn,
  input  clk,
  input  we,
  input  [1:0] addr
);

  wire and_1_out, and_2_out, and_3_out, and_4_out, decoder_2to4_1_y0, decoder_2to4_1_y1, decoder_2to4_1_y2,
       decoder_2to4_1_y3;

  decoder_2to4 decoder_2to4_1 (
    .a1(addr[1]), .a0(addr[0]), .y3(decoder_2to4_1_y3), .y2(decoder_2to4_1_y2), .y1(decoder_2to4_1_y1),
    .y0(decoder_2to4_1_y0));
  and and_1 (and_1_out, we, decoder_2to4_1_y0);
  and and_2 (and_2_out, we, decoder_2to4_1_y1);
  and and_3 (and_3_out, decoder_2to4_1_y2, we);
  and and_4 (and_4_out, we, decoder_2to4_1_y3);
  dff_8bit ram0 (.D(data), .RSTN(rstn), .CLK(clk), .EN(and_1_out), .CLR(1'b0));  // open: Q
  dff_8bit ram1 (.D(data), .RSTN(rstn), .CLK(clk), .EN(and_2_out), .CLR(1'b0));  // open: Q
  dff_8bit ram2 (.D(data), .RSTN(rstn), .CLK(clk), .EN(and_3_out), .CLR(1'b0));  // open: Q
  dff_8bit ram3 (.D(data), .RSTN(rstn), .CLK(clk), .EN(and_4_out), .CLR(1'b0));  // open: Q
endmodule
