// Logisim project comp_4bit.circ as structural Verilog: 1 circuit, main circuit comp_4bit
module comp_4bit (
  input  a3,
  input  a2,
  input  a1,
  input  a0,
  input  b3,
  input  b2,
  input  b1,
  input  b0,
  output cmp_o
);

  wire xnor_1_out, xnor_2_out, xnor_3_out, xnor_4_out;

  xnor xnor_1 (xnor_1_out, a3, b3);
  xnor xnor_2 (xnor_2_out, a2, b2);
  xnor xnor_3 (xnor_3_out, a1, b1);
  xnor xnor_4 (xnor_4_out, a0, b0);
  and and_1 (cmp_o, xnor_1_out, xnor_2_out, xnor_3_out, xnor_4_out);
endmodule
