// Logisim project dff_8bit.circ as structural Verilog: 6 circuits, main circuit dff_8bit
module dff_8bit (
  input  [7:0] D,
  input  RSTN,
  input  CLK,
  input  EN,
  input  CLR,
  output [7:0] Q
);

  dff_4bit dff_4bit_1 (
    .D3(D[7]), .D2(D[6]), .D1(D[5]), .D0(D[4]), .RSTN(RSTN), .CLK(CLK), .EN(EN), .CLR(CLR), .Q3(Q[7]),
    .Q2(Q[6]), .Q1(Q[5]), .Q0(Q[4]));
  dff_4bit dff_4bit_2 (
    .D3(D[3]), .D2(D[2]), .D1(D[1]), .D0(D[0]), .RSTN(RSTN), .CLK(CLK), .EN(EN), .CLR(CLR), .Q3(Q[3]),
    .Q2(Q[2]), .Q1(Q[1]), .Q0(Q[0]));
endmodule

module dff_4bit (
  input  D3,
  input  D2,
  input  D1,
  input  D0,
  input  RSTN,
  input  CLK,
  input  EN,
  input  CLR,
  output Q3,
  output Q2,
  output Q1,
  output Q0
);

  dff_enclr dff_enclr_1 (.d(D3), .en(EN), .clr(CLR), .clk(CLK), .rstn(RSTN), .q(Q3));
  dff_enclr dff_enclr_2 (.d(D2), .en(EN), .clr(CLR), .clk(CLK), .rstn(RSTN), .q(Q2));
  dff_enclr dff_enclr_3 (.d(D1), .en(EN), .clr(CLR), .clk(CLK), .rstn(RSTN), .q(Q1));
  dff_enclr dff_enclr_4 (.d(D0), .en(EN), .clr(CLR), .clk(CLK), .rstn(RSTN), .q(Q0));
endmodule

module dff_enclr (
  input  d,
  input  en,
  input  clr,
  input  clk,
  input  rstn,
  output q
);

  wire and_1_out, and_2_out, not_1_out, not_2_out, or_1_out, or_2_out;

  or or_1 (or_1_out, d, not_1_out);
  not not_1 (not_1_out, en);
  not not_2 (not_2_out, clr);
  or or_2 (or_2_out, en, q);
  and and_1 (and_1_out, not_2_out, and_2_out);
  and and_2 (and_2_out, or_1_out, or_2_out);
  dff dff_1 (.D(and_1_out), .CLK(clk), .rstn(rstn), .Q(q));
endmodule

module dff (
  input  D,
  input  CLK,
  input  rstn,
  output Q
);

  wire d_latch_rstn_1_q, not_1_out;

  not not_1 (not_1_out, CLK);
  d_latch_rstn d_latch_rstn_1 (.D(D), .WE(not_1_out), .rstn(rstn), .Q(d_latch_rstn_1_q));
  d_latch_rstn d_latch_rstn_2 (.D(d_latch_rstn_1_q), .WE(CLK), .rstn(rstn), .Q(Q));
endmodule

module d_latch_rstn (
  input  D,
  input  WE,
  input  rstn,
  output Q
);

  wire and_1_out, and_2_out, and_3_out, not_1_out, not_2_out, or_1_out;

  not not_1 (not_1_out, D);
  and and_1 (and_1_out, D, WE);
  and and_2 (and_2_out, WE, not_1_out);
  not not_2 (not_2_out, rstn);
  or or_1 (or_1_out, and_2_out, not_2_out);
  and and_3 (and_3_out, and_1_out, rstn);
  sr_latch sr_latch_1 (.R(or_1_out), .S(and_3_out), .Q(Q));  // open: Qn
endmodule

module sr_latch (
  input  R,
  input  S,
  output Q,
  output Qn
);

  nor nor_1 (Q, R, Qn);
  nor nor_2 (Qn, Q, S);
endmodule
