// Logisim project encoder_4-2.circ as structural Verilog: 1 circuit, main circuit encoder_4to2
module encoder_4to2 (
  input  a3,
  input  a2,
  input  a1,
  input  a0,
  output y1,
  output y0
);

  or or_1 (y1, a3, a2);
  or or_2 (y0, a3, a1);
endmodule
