// Logisim project full_adder_4bit.circ as structural Verilog: 2 circuits, main circuit x_full_adder_4bit
module x_full_adder_4bit_mux (
  input  a3,
  input  a2,
  input  a1,
  input  a0,
  input  b3,
  input  b2,
  input  b1,
  input  b0,
  input  cin,
  input  sel_b,
  output s3,
  output s2,
  output s1,
  output s0,
  output cout
);

  wire multiplexer_1_out, multiplexer_2_out, multiplexer_3_out, multiplexer_4_out, multiplexer_5_out,
       multiplexer_6_out, multiplexer_7_out, multiplexer_8_out;

  Multiplexer multiplexer_1 (.in0(a3), .in1(b3), .out(multiplexer_1_out), .sel(sel_b));
  Multiplexer multiplexer_2 (.in0(a2), .in1(b2), .out(multiplexer_2_out), .sel(sel_b));
  Multiplexer multiplexer_3 (.in0(a1), .in1(b1), .out(multiplexer_3_out), .sel(sel_b));
  Multiplexer multiplexer_4 (.in0(a0), .in1(b0), .out(multiplexer_4_out), .sel(sel_b));
  Multiplexer multiplexer_5 (.in0(b3), .in1(a3), .out(multiplexer_5_out), .sel(sel_b));
  Multiplexer multiplexer_6 (.in0(b2), .in1(a2), .out(multiplexer_6_out), .sel(sel_b));
  Multiplexer multiplexer_7 (.in0(b1), .in1(a1), .out(multiplexer_7_out), .sel(sel_b));
  Multiplexer multiplexer_8 (.in0(b0), .in1(a0), .out(multiplexer_8_out), .sel(sel_b));
  x_full_adder_4bit x_full_adder_4bit_1 (
    .a3(multiplexer_1_out), .a2(multiplexer_2_out), .a1(multiplexer_3_out), .a0(multiplexer_4_out),
    .b3(multiplexer_5_out), .b2(multiplexer_6_out), .b1(multiplexer_7_out), .b0(multiplexer_8_out),
    .cin(cin), .s3(s3), .s2(s2), .s1(s1), .s0(s0), .cout(cout));
endmodule

module x_full_adder_4bit (
  input  a3,
  input  a2,
  input  a1,
  input  a0,
  input  b3,
  input  b2,
  input  b1,
  input  b0,
  input  cin,
  output s3,
  output s2,
  output s1,
  output s0,
  output cout
);

  wire full_adder_1bit_2_cout, full_adder_1bit_3_cout, full_adder_1bit_4_cout;

  full_adder_1bit full_adder_1bit_1 (.a(a3), .b(b3), .cin(full_adder_1bit_2_cout), .s(s3), .cout(cout));
  full_adder_1bit full_adder_1bit_2 (
    .a(a2), .b(b2), .cin(full_adder_1bit_3_cout), .s(s2), .cout(full_adder_1bit_2_cout));
  full_adder_1bit full_adder_1bit_3 (
    .a(a1), .b(b1), .cin(full_adder_1bit_4_cout), .s(s1), .cout(full_adder_1bit_3_cout));
  full_adder_1bit full_adder_1bit_4 (.a(a0), .b(b0), .cin(cin), .s(s0), .cout(full_adder_1bit_4_cout));
endmodule
