// Logisim project full_sub_4bit.circ as structural Verilog: 3 circuits, main circuit full_sub_1bit
module full_sub_4bit_mux (
  input  a3,
  input  a2,
  input  a1,
  input  a0,
  input  b3,
  input  b2,
  input  b1,
  input  b0,
  input  cin,
  input  sel_b,
  output d3,
  output d2,
  output d1,
  output d0,
  output cout
);

  wire multiplexer_1_out, multiplexer_2_out, multiplexer_3_out, multiplexer_4_out, multiplexer_5_out,
       multiplexer_6_out, multiplexer_7_out, multiplexer_8_out;

  Multiplexer multiplexer_1 (.in0(a3), .in1(b3), .out(multiplexer_1_out), .sel(sel_b));
  Multiplexer multiplexer_2 (.in0(a2), .in1(b2), .out(multiplexer_2_out), .sel(sel_b));
  Multiplexer multiplexer_3 (.in0(a1), .in1(b1), .out(multiplexer_3_out), .sel(sel_b));
  Multiplexer multiplexer_4 (.in0(a0), .in1(b0), .out(multiplexer_4_out), .sel(sel_b));
  Multiplexer multiplexer_5 (.in0(b3), .in1(a3), .out(multiplexer_5_out), .sel(sel_b));
  Multiplexer multiplexer_6 (.in0(b2), .in1(a2), .out(multiplexer_6_out), .sel(sel_b));
  Multiplexer multiplexer_7 (.in0(b1), .in1(a1), .out(multiplexer_7_out), .sel(sel_b));
  Multiplexer multiplexer_8 (.in0(b0), .in1(a0), .out(multiplexer_8_out), .sel(sel_b));
  full_sub_4bit full_sub_4bit_1 (
    .a3(multiplexer_1_out), .a2(multiplexer_2_out), .a1(multiplexer_3_out), .a0(multiplexer_4_out),
    .b3(multiplexer_5_out), .b2(multiplexer_6_out), .b1(multiplexer_7_out), .b0(multiplexer_8_out),
    .cin(cin), .d3(d3), .d2(d2), .d1(d1), .d0(d0), .cout(cout));
endmodule

module full_sub_4bit (
  input  a3,
  input  a2,
  input  a1,
  input  a0,
  input  b3,
  input  b2,
  input  b1,
  input  b0,
  input  cin,
  output d3,
  output d2,
  output d1,
  output d0,
  output cout
);

  wire full_sub_1bit_2_cout, full_sub_1bit_3_cout, full_sub_1bit_4_cout;

  full_sub_1bit full_sub_1bit_1 (.a(a3), .b(b3), .cin(full_sub_1bit_2_cout), .d(d3), .cout(cout));
  full_sub_1bit full_sub_1bit_2 (.a(a2), .b(b2), .cin(full_sub_1bit_3_cout), .d(d2), .cout(full_sub_1bit_2_cout));
  full_sub_1bit full_sub_1bit_3 (.a(a1), .b(b1), .cin(full_sub_1bit_4_cout), .d(d1), .cout(full_sub_1bit_3_cout));
  full_sub_1bit full_sub_1bit_4 (.a(a0), .b(b0), .cin(cin), .d(d0), .cout(full_sub_1bit_4_cout));
endmodule

module full_sub_1bit (
  input  a,
  input  b,
  input  cin,
  output d,
  output cout
);

  wire and_1_out, and_2_out, not_1_out, not_2_out, xor_1_out;

  xor xor_1 (xor_1_out, a, b);
  not not_1 (not_1_out, a);
  not not_2 (not_2_out, xor_1_out);
  xor xor_2 (d, xor_1_out, cin);
  and and_1 (and_1_out, not_2_out, cin);
  and and_2 (and_2_out, not_1_out, b);
  or or_1 (cout, and_1_out, and_2_out);
endmodule
